// Logisim project basicgates.circ as structural Verilog: 45 circuits, main circuit main
module main (
);

  wire [63:0] multiplier_1_cout, multiplier_1_out;

  // Probe on multiplier_1_out
  Multiplier #(.width(64)) multiplier_1 (
    .a(64'hfffffffff), .b(64'hffffffffffffffee), .out(multiplier_1_out), .cin(64'h1234),
    .cout(multiplier_1_cout));
  // Probe on multiplier_1_cout
  // Probe on nothing
  // Probe on nothing
endmodule

module adder1bit (
  input  inflow,
  input  input1,
  input  input2,
  output overflow,
  output output1
);

  wire and_1_out, and_2_out, xor_1_out;

  and and_1 (and_1_out, input1, input2);
  xor xor_1 (xor_1_out, input1, input2);
  and and_2 (and_2_out, inflow, xor_1_out);
  xor xor_2 (output1, inflow, xor_1_out);
  or or_1 (overflow, and_1_out, and_2_out);
endmodule

module adder2bit (
  input  inflow,
  input  [1:0] input1,
  input  [1:0] input2,
  output overflow,
  output [1:0] output1
);

  wire adder1bit_1_overflow;

  adder1bit adder1bit_1 (
    .inflow(inflow), .input1(input1[0]), .input2(input2[0]), .overflow(adder1bit_1_overflow),
    .output1(output1[0]));
  adder1bit adder1bit_2 (
    .inflow(adder1bit_1_overflow), .input1(input1[1]), .input2(input2[1]), .overflow(overflow),
    .output1(output1[1]));
endmodule

module adder4bit (
  input  inflow,
  input  [3:0] input1,
  input  [3:0] input2,
  output overflow,
  output [3:0] output1
);

  wire adder2bit_1_overflow;

  adder2bit adder2bit_1 (
    .inflow(inflow), .input1(input1[1:0]), .input2(input2[1:0]), .overflow(adder2bit_1_overflow),
    .output1(output1[1:0]));
  adder2bit adder2bit_2 (
    .inflow(adder2bit_1_overflow), .input1(input1[3:2]), .input2(input2[3:2]), .overflow(overflow),
    .output1(output1[3:2]));
endmodule

module adder8bit (
  input  inflow,
  input  [7:0] input1,
  input  [7:0] input2,
  output overflow,
  output [7:0] output1
);

  wire adder4bit_1_overflow;

  adder4bit adder4bit_1 (
    .inflow(inflow), .input1(input1[3:0]), .input2(input2[3:0]), .overflow(adder4bit_1_overflow),
    .output1(output1[3:0]));
  adder4bit adder4bit_2 (
    .inflow(adder4bit_1_overflow), .input1(input1[7:4]), .input2(input2[7:4]), .overflow(overflow),
    .output1(output1[7:4]));
endmodule

module adder16bit (
  input  inflow,
  input  [15:0] input1,
  input  [15:0] input2,
  output overflow,
  output [15:0] output1
);

  wire adder8bit_1_overflow;

  adder8bit adder8bit_1 (
    .inflow(inflow), .input1(input1[7:0]), .input2(input2[7:0]), .overflow(adder8bit_1_overflow),
    .output1(output1[7:0]));
  adder8bit adder8bit_2 (
    .inflow(adder8bit_1_overflow), .input1(input1[15:8]), .input2(input2[15:8]), .overflow(overflow),
    .output1(output1[15:8]));
endmodule

module adder32bit (
  input  inflow,
  input  [31:0] input1,
  input  [31:0] input2,
  output overflow,
  output [31:0] output1
);

  wire adder16bit_1_overflow;

  adder16bit adder16bit_1 (
    .inflow(inflow), .input1(input1[15:0]), .input2(input2[15:0]), .overflow(adder16bit_1_overflow),
    .output1(output1[15:0]));
  adder16bit adder16bit_2 (
    .inflow(adder16bit_1_overflow), .input1(input1[31:16]), .input2(input2[31:16]), .overflow(overflow),
    .output1(output1[31:16]));
endmodule

module adder64bit (
  input  inflow,
  input  [63:0] input1,
  input  [63:0] input2,
  output overflow,
  output [63:0] output1
);

  wire adder32bit_1_overflow;

  adder32bit adder32bit_1 (
    .inflow(inflow), .input1(input1[31:0]), .input2(input2[31:0]), .overflow(adder32bit_1_overflow),
    .output1(output1[31:0]));
  adder32bit adder32bit_2 (
    .inflow(adder32bit_1_overflow), .input1(input1[63:32]), .input2(input2[63:32]), .overflow(overflow),
    .output1(output1[63:32]));
endmodule

module negate1bit (
  input  input1,
  output output1
);


  assign output1 = input1;
endmodule

module negate2bit (
  input  [1:0] input1,
  output [1:0] output1
);

  wire [1:0] not_1_out;

  assign not_1_out = ~input1;  // NOT_Gate not_1, 2 bits wide
  adder2bit adder2bit_1 (.input1(2'b01), .input2(not_1_out), .output1(output1));  // open: inflow, overflow
endmodule

module negate4bit (
  input  [3:0] input1,
  output [3:0] output1
);

  wire [3:0] not_1_out;

  assign not_1_out = ~input1;  // NOT_Gate not_1, 4 bits wide
  adder4bit adder4bit_1 (.input1(4'b0001), .input2(not_1_out), .output1(output1));  // open: inflow, overflow
endmodule

module negate8bit (
  input  [7:0] input1,
  output [7:0] output1
);

  wire [7:0] not_1_out;

  assign not_1_out = ~input1;  // NOT_Gate not_1, 8 bits wide
  adder8bit adder8bit_1 (.input1(8'h1), .input2(not_1_out), .output1(output1));  // open: inflow, overflow
endmodule

module negate16bit (
  input  [15:0] input1,
  output [15:0] output1
);

  wire [15:0] not_1_out;

  assign not_1_out = ~input1;  // NOT_Gate not_1, 16 bits wide
  adder16bit adder16bit_1 (.input1(16'h1), .input2(not_1_out), .output1(output1));  // open: inflow, overflow
endmodule

module negate32bit (
  input  [31:0] input1,
  output [31:0] output1
);

  wire [31:0] not_1_out;

  assign not_1_out = ~input1;  // NOT_Gate not_1, 32 bits wide
  adder32bit adder32bit_1 (.input1(32'h1), .input2(not_1_out), .output1(output1));  // open: inflow, overflow
endmodule

module negate64bit (
  input  [63:0] input1,
  output [63:0] output1
);

  wire [63:0] not_1_out;

  assign not_1_out = ~input1;  // NOT_Gate not_1, 64 bits wide
  adder64bit adder64bit_1 (.input1(64'h1), .input2(not_1_out), .output1(output1));  // open: inflow, overflow
endmodule

module subtractor1bit (
  input  inborrow,
  input  input1,
  input  input2,
  output borrow,
  output output1
);

  wire and_1_out, and_2_out, not_1_out, not_2_out, xor_1_out;

  not not_1 (not_1_out, input1);
  xor xor_1 (xor_1_out, input1, input2);
  and and_1 (and_1_out, not_1_out, input2);
  and and_2 (and_2_out, inborrow, not_2_out);
  not not_2 (not_2_out, xor_1_out);
  xor xor_2 (output1, inborrow, xor_1_out);
  or or_1 (borrow, and_1_out, and_2_out);
endmodule

module subtractor2bit (
  input  inborrow,
  input  [1:0] input1,
  input  [1:0] input2,
  output borrow,
  output [1:0] output1
);

  wire subtractor1bit_1_borrow;

  subtractor1bit subtractor1bit_1 (
    .inborrow(inborrow), .input1(input1[0]), .input2(input2[0]), .borrow(subtractor1bit_1_borrow),
    .output1(output1[0]));
  subtractor1bit subtractor1bit_2 (
    .inborrow(subtractor1bit_1_borrow), .input1(input1[1]), .input2(input2[1]), .borrow(borrow),
    .output1(output1[1]));
endmodule

module subtractor4bit (
  input  inborrow,
  input  [3:0] input1,
  input  [3:0] input2,
  output borrow,
  output [3:0] output1
);

  wire subtractor2bit_1_borrow;

  subtractor2bit subtractor2bit_1 (
    .inborrow(inborrow), .input1(input1[1:0]), .input2(input2[1:0]), .borrow(subtractor2bit_1_borrow),
    .output1(output1[1:0]));
  subtractor2bit subtractor2bit_2 (
    .inborrow(subtractor2bit_1_borrow), .input1(input1[3:2]), .input2(input2[3:2]), .borrow(borrow),
    .output1(output1[3:2]));
endmodule

module subtractor8bit (
  input  inborrow,
  input  [7:0] input1,
  input  [7:0] input2,
  output borrow,
  output [7:0] output1
);

  wire subtractor4bit_1_borrow;

  subtractor4bit subtractor4bit_1 (
    .inborrow(inborrow), .input1(input1[3:0]), .input2(input2[3:0]), .borrow(subtractor4bit_1_borrow),
    .output1(output1[3:0]));
  subtractor4bit subtractor4bit_2 (
    .inborrow(subtractor4bit_1_borrow), .input1(input1[7:4]), .input2(input2[7:4]), .borrow(borrow),
    .output1(output1[7:4]));
endmodule

module subtractor16bit (
  input  inborrow,
  input  [15:0] input1,
  input  [15:0] input2,
  output borrow,
  output [15:0] output1
);

  wire subtractor8bit_1_borrow;

  subtractor8bit subtractor8bit_1 (
    .inborrow(inborrow), .input1(input1[7:0]), .input2(input2[7:0]), .borrow(subtractor8bit_1_borrow),
    .output1(output1[7:0]));
  subtractor8bit subtractor8bit_2 (
    .inborrow(subtractor8bit_1_borrow), .input1(input1[15:8]), .input2(input2[15:8]), .borrow(borrow),
    .output1(output1[15:8]));
endmodule

module subtractor32bit (
  input  inborrow,
  input  [31:0] input1,
  input  [31:0] input2,
  output borrow,
  output [31:0] output1
);

  wire subtractor16bit_1_borrow;

  subtractor16bit subtractor16bit_1 (
    .inborrow(inborrow), .input1(input1[15:0]), .input2(input2[15:0]), .borrow(subtractor16bit_1_borrow),
    .output1(output1[15:0]));
  subtractor16bit subtractor16bit_2 (
    .inborrow(subtractor16bit_1_borrow), .input1(input1[31:16]), .input2(input2[31:16]), .borrow(borrow),
    .output1(output1[31:16]));
endmodule

module subtractor64bit (
  input  inborrow,
  input  [63:0] input1,
  input  [63:0] input2,
  output borrow,
  output [63:0] output1
);

  wire subtractor32bit_1_borrow;

  subtractor32bit subtractor32bit_1 (
    .inborrow(inborrow), .input1(input1[31:0]), .input2(input2[31:0]), .borrow(subtractor32bit_1_borrow),
    .output1(output1[31:0]));
  subtractor32bit subtractor32bit_2 (
    .inborrow(subtractor32bit_1_borrow), .input1(input1[63:32]), .input2(input2[63:32]), .borrow(borrow),
    .output1(output1[63:32]));
endmodule

module adder128bit (
  input  inflow,
  input  [63:0] input1a,
  input  [63:0] input1b,
  input  [63:0] input2a,
  input  [63:0] input2b,
  output overflow,
  output [63:0] output1a,
  output [63:0] output1b
);

  wire adder64bit_1_overflow;

  adder64bit adder64bit_1 (
    .inflow(inflow), .input1(input1a), .input2(input2a), .overflow(adder64bit_1_overflow), .output1(output1a));
  adder64bit adder64bit_2 (
    .inflow(adder64bit_1_overflow), .input1(input1b), .input2(input2b), .overflow(overflow),
    .output1(output1b));
endmodule

module negate128bit (
  input  [63:0] input1a,
  input  [63:0] input1b,
  output [63:0] output1a,
  output [63:0] output1b
);

  wire [63:0] not_1_out, not_2_out;

  assign not_1_out = ~input1a;  // NOT_Gate not_1, 64 bits wide
  assign not_2_out = ~input1b;  // NOT_Gate not_2, 64 bits wide
  adder128bit adder128bit_1 (
    .input1a(64'h1), .input2a(not_1_out), .input2b(not_2_out), .output1a(output1a), .output1b(output1b));  // open: inflow, input1b, overflow
endmodule

module subtractor128bit (
  input  inborrow,
  input  [63:0] input1a,
  input  [63:0] input1b,
  input  [63:0] input2a,
  input  [63:0] input2b,
  output borrow,
  output [63:0] output1a,
  output [63:0] output1b
);

  wire subtractor64bit_1_borrow;

  subtractor64bit subtractor64bit_1 (
    .inborrow(inborrow), .input1(input1a), .input2(input2a), .borrow(subtractor64bit_1_borrow),
    .output1(output1a));
  subtractor64bit subtractor64bit_2 (
    .inborrow(subtractor64bit_1_borrow), .input1(input1b), .input2(input2b), .borrow(borrow),
    .output1(output1b));
endmodule

module cbuffer1bit (
  input  buffer1,
  input  input1,
  output output1
);

  and and_1 (output1, buffer1, input1);
endmodule

module cbuffer2bit (
  input  buffer1,
  input  [1:0] input1,
  output [1:0] output1
);

  assign output1 = {2{buffer1}} & input1;  // AND_Gate and_1, 2 bits wide
endmodule

module cbuffer4bit (
  input  buffer1,
  input  [3:0] input1,
  output [3:0] output1
);

  assign output1 = {4{buffer1}} & input1;  // AND_Gate and_1, 4 bits wide
endmodule

module cbuffer8bit (
  input  buffer1,
  input  [7:0] input1,
  output [7:0] output1
);

  assign output1 = {8{buffer1}} & input1;  // AND_Gate and_1, 8 bits wide
endmodule

module cbuffer16bit (
  input  buffer1,
  input  [15:0] input1,
  output [15:0] output1
);

  assign output1 = {16{buffer1}} & input1;  // AND_Gate and_1, 16 bits wide
endmodule

module cbuffer32bit (
  input  buffer1,
  input  [31:0] input1,
  output [31:0] output1
);

  assign output1 = {32{buffer1}} & input1;  // AND_Gate and_1, 32 bits wide
endmodule

module cbuffer64bit (
  input  buffer1,
  input  [63:0] input1,
  output [63:0] output1
);

  assign output1 = {64{buffer1}} & input1;  // AND_Gate and_1, 64 bits wide
endmodule

module cbuffer128bit (
  input  buffer1,
  input  [63:0] input1a,
  input  [63:0] input1b,
  output [63:0] output1a,
  output [63:0] output1b
);

  assign output1a = {64{buffer1}} & input1a;  // AND_Gate and_1, 64 bits wide
  assign output1b = {64{buffer1}} & input1b;  // AND_Gate and_2, 64 bits wide
endmodule

module multiplier1bit (
  input  inflow,
  input  input1,
  input  input2,
  output overflow,
  output output1
);

  wire and_1_out;

  and and_1 (and_1_out, input1, input2);
  xor xor_1 (output1, inflow, and_1_out);
  and and_2 (overflow, inflow, and_1_out);
endmodule

module multiplier2bit (
  input  [1:0] inflow,
  input  [1:0] input1,
  input  [1:0] input2,
  output [1:0] overflow,
  output [1:0] output1
);

  wire [3:0] adder4bit_2_output1, cbuffer4bit_1_output1, cbuffer4bit_2_output1;

  adder4bit adder4bit_1 (
    .input1({2'b00, inflow}), .input2(adder4bit_2_output1), .output1({overflow, output1}));  // open: inflow, overflow
  cbuffer4bit cbuffer4bit_1 (.buffer1(input1[0]), .input1({2'b00, input2}), .output1(cbuffer4bit_1_output1));
  adder4bit adder4bit_2 (
    .input1(cbuffer4bit_1_output1), .input2(cbuffer4bit_2_output1), .output1(adder4bit_2_output1));  // open: inflow, overflow
  cbuffer4bit cbuffer4bit_2 (.buffer1(input1[1]), .input1({1'b0, input2, 1'b0}), .output1(cbuffer4bit_2_output1));
endmodule

module multiplier4bit (
  input  [3:0] inflow,
  input  [3:0] input1,
  input  [3:0] input2,
  output [3:0] overflow,
  output [3:0] output1
);

  wire [1:0] multiplier2bit_1_output1, multiplier2bit_1_overflow;
  wire [5:2] multiplier2bit_2_output1, multiplier2bit_3_output1;
  wire [7:0] adder8bit_1_output1, adder8bit_3_output1, adder8bit_4_output1;
  wire [7:4] multiplier2bit_4_output1;

  adder8bit adder8bit_1 (
    .input1({4'b0000, multiplier2bit_1_overflow, multiplier2bit_1_output1}),
    .input2({2'b00, multiplier2bit_2_output1, 2'b00}), .output1(adder8bit_1_output1));  // open: inflow, overflow
  multiplier2bit multiplier2bit_1 (
    .input1(input1[1:0]), .input2(input2[1:0]), .overflow(multiplier2bit_1_overflow),
    .output1(multiplier2bit_1_output1));  // open: inflow
  adder8bit adder8bit_2 (
    .input1({4'b0000, inflow}), .input2(adder8bit_3_output1), .output1({overflow, output1}));  // open: inflow, overflow
  adder8bit adder8bit_3 (
    .input1(adder8bit_1_output1), .input2(adder8bit_4_output1), .output1(adder8bit_3_output1));  // open: inflow, overflow
  adder8bit adder8bit_4 (
    .input1({2'b00, multiplier2bit_3_output1, 2'b00}), .input2({multiplier2bit_4_output1, 4'b0000}),
    .output1(adder8bit_4_output1));  // open: inflow, overflow
  multiplier2bit multiplier2bit_2 (
    .input1(input1[1:0]), .input2(input2[3:2]), .overflow(multiplier2bit_2_output1[5:4]),
    .output1(multiplier2bit_2_output1[3:2]));  // open: inflow
  multiplier2bit multiplier2bit_3 (
    .input1(input1[3:2]), .input2(input2[1:0]), .overflow(multiplier2bit_3_output1[5:4]),
    .output1(multiplier2bit_3_output1[3:2]));  // open: inflow
  multiplier2bit multiplier2bit_4 (
    .input1(input1[3:2]), .input2(input2[3:2]), .overflow(multiplier2bit_4_output1[7:6]),
    .output1(multiplier2bit_4_output1[5:4]));  // open: inflow
endmodule

module multiplier8bit (
  input  [7:0] inflow,
  input  [7:0] input1,
  input  [7:0] input2,
  output [7:0] overflow,
  output [7:0] output1
);

  wire [3:0] multiplier4bit_1_output1, multiplier4bit_1_overflow;
  wire [11:4] multiplier4bit_2_output1, multiplier4bit_3_output1;
  wire [15:0] adder16bit_1_output1, adder16bit_3_output1, adder16bit_4_output1;
  wire [15:8] multiplier4bit_4_output1;

  adder16bit adder16bit_1 (
    .input1({{8{1'b0}}, multiplier4bit_1_overflow, multiplier4bit_1_output1}),
    .input2({4'b0000, multiplier4bit_2_output1, 4'b0000}), .output1(adder16bit_1_output1));  // open: inflow, overflow
  multiplier4bit multiplier4bit_1 (
    .input1(input1[3:0]), .input2(input2[3:0]), .overflow(multiplier4bit_1_overflow),
    .output1(multiplier4bit_1_output1));  // open: inflow
  adder16bit adder16bit_2 (
    .input1({{8{1'b0}}, inflow}), .input2(adder16bit_3_output1), .output1({overflow, output1}));  // open: inflow, overflow
  adder16bit adder16bit_3 (
    .input1(adder16bit_1_output1), .input2(adder16bit_4_output1), .output1(adder16bit_3_output1));  // open: inflow, overflow
  adder16bit adder16bit_4 (
    .input1({4'b0000, multiplier4bit_3_output1, 4'b0000}), .input2({multiplier4bit_4_output1, {8{1'b0}}}),
    .output1(adder16bit_4_output1));  // open: inflow, overflow
  multiplier4bit multiplier4bit_2 (
    .input1(input1[3:0]), .input2(input2[7:4]), .overflow(multiplier4bit_2_output1[11:8]),
    .output1(multiplier4bit_2_output1[7:4]));  // open: inflow
  multiplier4bit multiplier4bit_3 (
    .input1(input1[7:4]), .input2(input2[3:0]), .overflow(multiplier4bit_3_output1[11:8]),
    .output1(multiplier4bit_3_output1[7:4]));  // open: inflow
  multiplier4bit multiplier4bit_4 (
    .input1(input1[7:4]), .input2(input2[7:4]), .overflow(multiplier4bit_4_output1[15:12]),
    .output1(multiplier4bit_4_output1[11:8]));  // open: inflow
endmodule

module multiplier16bit (
  input  [15:0] inflow,
  input  [15:0] input1,
  input  [15:0] input2,
  output [15:0] overflow,
  output [15:0] output1
);

  wire [7:0] multiplier8bit_1_output1, multiplier8bit_1_overflow;
  wire [23:8] multiplier8bit_2_output1, multiplier8bit_3_output1;
  wire [31:0] adder32bit_1_output1, adder32bit_3_output1, adder32bit_4_output1;
  wire [31:16] multiplier8bit_4_output1;

  adder32bit adder32bit_1 (
    .input1({{16{1'b0}}, multiplier8bit_1_overflow, multiplier8bit_1_output1}),
    .input2({{8{1'b0}}, multiplier8bit_2_output1, {8{1'b0}}}), .output1(adder32bit_1_output1));  // open: inflow, overflow
  multiplier8bit multiplier8bit_1 (
    .input1(input1[7:0]), .input2(input2[7:0]), .overflow(multiplier8bit_1_overflow),
    .output1(multiplier8bit_1_output1));  // open: inflow
  adder32bit adder32bit_2 (
    .input1({{16{1'b0}}, inflow}), .input2(adder32bit_3_output1), .output1({overflow, output1}));  // open: inflow, overflow
  adder32bit adder32bit_3 (
    .input1(adder32bit_1_output1), .input2(adder32bit_4_output1), .output1(adder32bit_3_output1));  // open: inflow, overflow
  adder32bit adder32bit_4 (
    .input1({{8{1'b0}}, multiplier8bit_3_output1, {8{1'b0}}}),
    .input2({multiplier8bit_4_output1, {16{1'b0}}}), .output1(adder32bit_4_output1));  // open: inflow, overflow
  multiplier8bit multiplier8bit_2 (
    .input1(input1[7:0]), .input2(input2[15:8]), .overflow(multiplier8bit_2_output1[23:16]),
    .output1(multiplier8bit_2_output1[15:8]));  // open: inflow
  multiplier8bit multiplier8bit_3 (
    .input1(input1[15:8]), .input2(input2[7:0]), .overflow(multiplier8bit_3_output1[23:16]),
    .output1(multiplier8bit_3_output1[15:8]));  // open: inflow
  multiplier8bit multiplier8bit_4 (
    .input1(input1[15:8]), .input2(input2[15:8]), .overflow(multiplier8bit_4_output1[31:24]),
    .output1(multiplier8bit_4_output1[23:16]));  // open: inflow
endmodule

module multiplier32bit (
  input  [31:0] inflow,
  input  [31:0] input1,
  input  [31:0] input2,
  output [31:0] overflow,
  output [31:0] output1
);

  wire [15:0] multiplier16bit_1_output1, multiplier16bit_1_overflow;
  wire [47:16] multiplier16bit_2_output1, multiplier16bit_3_output1;
  wire [63:0] adder64bit_1_output1, adder64bit_3_output1, adder64bit_4_output1;
  wire [63:32] multiplier16bit_4_output1;

  adder64bit adder64bit_1 (
    .input1({{32{1'b0}}, multiplier16bit_1_overflow, multiplier16bit_1_output1}),
    .input2({{16{1'b0}}, multiplier16bit_2_output1, {16{1'b0}}}), .output1(adder64bit_1_output1));  // open: inflow, overflow
  multiplier16bit multiplier16bit_1 (
    .input1(input1[15:0]), .input2(input2[15:0]), .overflow(multiplier16bit_1_overflow),
    .output1(multiplier16bit_1_output1));  // open: inflow
  adder64bit adder64bit_2 (
    .input1({{32{1'b0}}, inflow}), .input2(adder64bit_3_output1), .output1({overflow, output1}));  // open: inflow, overflow
  adder64bit adder64bit_3 (
    .input1(adder64bit_1_output1), .input2(adder64bit_4_output1), .output1(adder64bit_3_output1));  // open: inflow, overflow
  adder64bit adder64bit_4 (
    .input1({{16{1'b0}}, multiplier16bit_3_output1, {16{1'b0}}}),
    .input2({multiplier16bit_4_output1, {32{1'b0}}}), .output1(adder64bit_4_output1));  // open: inflow, overflow
  multiplier16bit multiplier16bit_2 (
    .input1(input1[15:0]), .input2(input2[31:16]), .overflow(multiplier16bit_2_output1[47:32]),
    .output1(multiplier16bit_2_output1[31:16]));  // open: inflow
  multiplier16bit multiplier16bit_3 (
    .input1(input1[31:16]), .input2(input2[15:0]), .overflow(multiplier16bit_3_output1[47:32]),
    .output1(multiplier16bit_3_output1[31:16]));  // open: inflow
  multiplier16bit multiplier16bit_4 (
    .input1(input1[31:16]), .input2(input2[31:16]), .overflow(multiplier16bit_4_output1[63:48]),
    .output1(multiplier16bit_4_output1[47:32]));  // open: inflow
endmodule

module multiplier64bit (
  input  [63:0] inflow,
  input  [63:0] input1,
  input  [63:0] input2,
  output [63:0] overflow,
  output [63:0] output1
);

  wire [31:0] multiplier32bit_2_overflow, multiplier32bit_3_overflow;
  wire [63:0] adder128bit_1_output1a, adder128bit_1_output1b, adder128bit_3_output1a, adder128bit_3_output1b,
       adder128bit_4_output1a, adder128bit_4_output1b, multiplier32bit_1_output1, multiplier32bit_4_output1;
  wire [63:32] multiplier32bit_2_output1, multiplier32bit_3_output1;

  adder128bit adder128bit_1 (
    .input1a(multiplier32bit_1_output1), .input1b({64{1'b0}}),
    .input2a({multiplier32bit_2_output1, {32{1'b0}}}), .input2b({{32{1'b0}}, multiplier32bit_2_overflow}),
    .output1a(adder128bit_1_output1a), .output1b(adder128bit_1_output1b));  // open: inflow, overflow
  multiplier32bit multiplier32bit_1 (
    .input1(input1[31:0]), .input2(input2[31:0]), .overflow(multiplier32bit_1_output1[63:32]),
    .output1(multiplier32bit_1_output1[31:0]));  // open: inflow
  adder128bit adder128bit_2 (
    .input1a(inflow), .input2a(adder128bit_3_output1a), .input2b(adder128bit_3_output1b), .output1a(output1),
    .output1b(overflow));  // open: inflow, input1b, overflow
  adder128bit adder128bit_3 (
    .input1a(adder128bit_1_output1a), .input1b(adder128bit_1_output1b), .input2a(adder128bit_4_output1a),
    .input2b(adder128bit_4_output1b), .output1a(adder128bit_3_output1a), .output1b(adder128bit_3_output1b));  // open: inflow, overflow
  multiplier32bit multiplier32bit_2 (
    .input1(input1[31:0]), .input2(input2[63:32]), .overflow(multiplier32bit_2_overflow),
    .output1(multiplier32bit_2_output1));  // open: inflow
  adder128bit adder128bit_4 (
    .input1a({multiplier32bit_3_output1, {32{1'b0}}}), .input1b({{32{1'b0}}, multiplier32bit_3_overflow}),
    .input2a({64{1'b0}}), .input2b(multiplier32bit_4_output1), .output1a(adder128bit_4_output1a),
    .output1b(adder128bit_4_output1b));  // open: inflow, overflow
  multiplier32bit multiplier32bit_3 (
    .input1(input1[63:32]), .input2(input2[31:0]), .overflow(multiplier32bit_3_overflow),
    .output1(multiplier32bit_3_output1));  // open: inflow
  multiplier32bit multiplier32bit_4 (
    .input1(input1[63:32]), .input2(input2[63:32]), .overflow(multiplier32bit_4_output1[63:32]),
    .output1(multiplier32bit_4_output1[31:0]));  // open: inflow
endmodule

module divider1bit (
  input  inupper,
  input  input1,
  input  input2,
  output remainder,
  output output1
);


  assign output1 = input1;
  assign remainder = 1'b0;
endmodule

module divideru2bit (
  input  [1:0] inupper,
  input  [1:0] input1,
  input  [1:0] input2,
  output [1:0] remainder,
  output [1:0] output1
);

  wire comparator_1_eq, comparator_2_eq, comparator_2_gt, comparator_3_eq, comparator_3_gt, comparator_4_eq,
       comparator_4_gt, comparator_5_eq, comparator_5_gt, not_1_out, or_1_out, or_2_out, or_3_out, or_4_out;
  wire [1:0] divider_1_out, divider_1_rem;
  wire [3:2] and_2_out;
  wire [7:0] cbuffer8bit_1_output1, cbuffer8bit_2_output1, cbuffer8bit_3_output1, cbuffer8bit_4_output1,
       subtractor8bit_1_output1, subtractor8bit_2_output1, subtractor8bit_3_output1;
  wire [7:2] subtractor8bit_4_output1;

  // Probe on inupper
  // Probe on inupper
  // Probe on input1
  // Probe on input1
  Comparator #(.mode("unsigned"), .width(2)) comparator_1 (
    .a(input2), .b(2'b00), .eq(comparator_1_eq));  // open: gt, lt
  // Probe on input2
  // Probe on input2
  not not_1 (not_1_out, comparator_1_eq);
  // Probe on divider_1_out
  // Probe on divider_1_out
  Divider #(.width(2)) divider_1 (.a(input1), .b(input2), .out(divider_1_out), .upper(inupper), .rem(divider_1_rem));
  // Probe on divider_1_rem
  // Probe on divider_1_rem
  or or_1 (or_1_out, comparator_2_gt, comparator_2_eq);
  Comparator #(.mode("unsigned")) comparator_2 (
    .a({4'b0000, inupper, input1}), .b({3'b000, input2, 3'b000}), .gt(comparator_2_gt), .eq(comparator_2_eq));  // open: lt
  cbuffer8bit cbuffer8bit_1 (
    .buffer1(and_2_out[3]), .input1({3'b000, input2, 3'b000}), .output1(cbuffer8bit_1_output1));
  and and_1 (and_2_out[3], or_1_out, not_1_out);
  subtractor8bit subtractor8bit_1 (
    .input1({4'b0000, inupper, input1}), .input2(cbuffer8bit_1_output1), .output1(subtractor8bit_1_output1));  // open: inborrow, borrow
  cbuffer8bit cbuffer8bit_2 (
    .buffer1(and_2_out[2]), .input1({4'b0000, input2, 2'b00}), .output1(cbuffer8bit_2_output1));
  and and_2 (and_2_out[2], or_2_out, not_1_out);
  or or_2 (or_2_out, comparator_3_gt, comparator_3_eq);
  Comparator #(.mode("unsigned")) comparator_3 (
    .a(subtractor8bit_1_output1), .b({4'b0000, input2, 2'b00}), .gt(comparator_3_gt), .eq(comparator_3_eq));  // open: lt
  // Probe on subtractor8bit_2_output1
  // Probe on subtractor8bit_2_output1
  subtractor8bit subtractor8bit_2 (
    .input1(subtractor8bit_1_output1), .input2(cbuffer8bit_2_output1), .output1(subtractor8bit_2_output1));  // open: inborrow, borrow
  cbuffer8bit cbuffer8bit_3 (.buffer1(output1[1]), .input1({{5{1'b0}}, input2, 1'b0}), .output1(cbuffer8bit_3_output1));
  and and_3 (output1[1], or_3_out, not_1_out);
  or or_3 (or_3_out, comparator_4_gt, comparator_4_eq);
  Comparator #(.mode("unsigned")) comparator_4 (
    .a(subtractor8bit_2_output1), .b({{5{1'b0}}, input2, 1'b0}), .gt(comparator_4_gt), .eq(comparator_4_eq));  // open: lt
  // Probe on subtractor8bit_3_output1
  // Probe on subtractor8bit_3_output1
  subtractor8bit subtractor8bit_3 (
    .input1(subtractor8bit_2_output1), .input2(cbuffer8bit_3_output1), .output1(subtractor8bit_3_output1));  // open: inborrow, borrow
  cbuffer8bit cbuffer8bit_4 (.buffer1(output1[0]), .input1({{6{1'b0}}, input2}), .output1(cbuffer8bit_4_output1));
  and and_4 (output1[0], or_4_out, not_1_out);
  or or_4 (or_4_out, comparator_5_gt, comparator_5_eq);
  Comparator #(.mode("unsigned")) comparator_5 (
    .a(subtractor8bit_3_output1), .b({{6{1'b0}}, input2}), .gt(comparator_5_gt), .eq(comparator_5_eq));  // open: lt
  // Probe on {subtractor8bit_4_output1, remainder}
  // Probe on {subtractor8bit_4_output1, remainder}
  subtractor8bit subtractor8bit_4 (
    .input1(subtractor8bit_3_output1), .input2(cbuffer8bit_4_output1),
    .output1({subtractor8bit_4_output1, remainder}));  // open: inborrow, borrow
  // Probe on {subtractor8bit_4_output1, remainder}
  // Probe on {subtractor8bit_4_output1, remainder}
  // Probe on {4'b0000, and_2_out, output1}
  // Probe on {4'b0000, and_2_out, output1}
  // Probe on remainder
  // Probe on remainder
  // Probe on output1
  // Probe on output1
endmodule

module divider2bit (
  input  [1:0] inupper,
  input  [1:0] input1,
  input  [1:0] input2,
  output [1:0] remainder,
  output [1:0] output1
);

  wire comparator_1_lt, comparator_2_lt, not_1_out, not_2_out, not_3_out, not_4_out, not_5_out, xor_1_out;
  wire [1:0] cbuffer2bit_1_output1, cbuffer2bit_2_output1, cbuffer2bit_3_output1, cbuffer2bit_4_output1,
       cbuffer2bit_5_output1, cbuffer2bit_6_output1, cbuffer2bit_7_output1, cbuffer2bit_8_output1,
       cbuffer2bit_9_output1, cbuffer2bit_10_output1, divider_1_out, divider_1_rem, divideru2bit_1_output1,
       divideru2bit_1_remainder, negate2bit_1_output1, negate2bit_2_output1, negate2bit_3_output1,
       negate2bit_4_output1, negate2bit_5_output1, or_1_out, or_2_out, or_3_out;

  // Probe on inupper
  // Probe on inupper
  // Probe on input1
  // Probe on input1
  // Probe on input2
  // Probe on input2
  // Probe on divider_1_out
  // Probe on divider_1_out
  Divider #(.mode("twosComplement"), .width(2)) divider_1 (
    .a(input1), .b(input2), .out(divider_1_out), .upper(inupper), .rem(divider_1_rem));
  // Probe on divider_1_rem
  // Probe on divider_1_rem
  Comparator #(.width(2)) comparator_1 (.a(input1), .b(2'b00), .lt(comparator_1_lt));  // open: gt, eq
  Comparator #(.width(2)) comparator_2 (.a(input2), .b(2'b00), .lt(comparator_2_lt));  // open: gt, eq
  negate2bit negate2bit_1 (.input1(inupper), .output1(negate2bit_1_output1));
  negate2bit negate2bit_2 (.input1(input1), .output1(negate2bit_2_output1));
  negate2bit negate2bit_3 (.input1(input2), .output1(negate2bit_3_output1));
  not not_1 (not_1_out, comparator_1_lt);
  not not_2 (not_2_out, comparator_1_lt);
  not not_3 (not_3_out, comparator_2_lt);
  cbuffer2bit cbuffer2bit_1 (.buffer1(not_1_out), .input1(inupper), .output1(cbuffer2bit_1_output1));
  cbuffer2bit cbuffer2bit_2 (.buffer1(comparator_1_lt), .input1(negate2bit_1_output1), .output1(cbuffer2bit_2_output1));
  cbuffer2bit cbuffer2bit_3 (.buffer1(not_2_out), .input1(input1), .output1(cbuffer2bit_3_output1));
  cbuffer2bit cbuffer2bit_4 (.buffer1(comparator_1_lt), .input1(negate2bit_2_output1), .output1(cbuffer2bit_4_output1));
  cbuffer2bit cbuffer2bit_5 (.buffer1(not_3_out), .input1(input2), .output1(cbuffer2bit_5_output1));
  cbuffer2bit cbuffer2bit_6 (.buffer1(comparator_2_lt), .input1(negate2bit_3_output1), .output1(cbuffer2bit_6_output1));
  assign or_1_out = cbuffer2bit_1_output1 | cbuffer2bit_2_output1;  // OR_Gate or_1, 2 bits wide
  assign or_2_out = cbuffer2bit_3_output1 | cbuffer2bit_4_output1;  // OR_Gate or_2, 2 bits wide
  assign or_3_out = cbuffer2bit_5_output1 | cbuffer2bit_6_output1;  // OR_Gate or_3, 2 bits wide
  xor xor_1 (xor_1_out, comparator_1_lt, comparator_2_lt);
  divideru2bit divideru2bit_1 (
    .inupper(or_1_out), .input1(or_2_out), .input2(or_3_out), .remainder(divideru2bit_1_remainder),
    .output1(divideru2bit_1_output1));
  negate2bit negate2bit_4 (.input1(divideru2bit_1_remainder), .output1(negate2bit_4_output1));
  negate2bit negate2bit_5 (.input1(divideru2bit_1_output1), .output1(negate2bit_5_output1));
  not not_4 (not_4_out, comparator_1_lt);
  not not_5 (not_5_out, xor_1_out);
  cbuffer2bit cbuffer2bit_7 (.buffer1(not_4_out), .input1(divideru2bit_1_remainder), .output1(cbuffer2bit_7_output1));
  cbuffer2bit cbuffer2bit_8 (.buffer1(comparator_1_lt), .input1(negate2bit_4_output1), .output1(cbuffer2bit_8_output1));
  cbuffer2bit cbuffer2bit_9 (.buffer1(not_5_out), .input1(divideru2bit_1_output1), .output1(cbuffer2bit_9_output1));
  cbuffer2bit cbuffer2bit_10 (.buffer1(xor_1_out), .input1(negate2bit_5_output1), .output1(cbuffer2bit_10_output1));
  assign remainder = cbuffer2bit_7_output1 | cbuffer2bit_8_output1;  // OR_Gate or_4, 2 bits wide
  assign output1 = cbuffer2bit_9_output1 | cbuffer2bit_10_output1;  // OR_Gate or_5, 2 bits wide
  // Probe on remainder
  // Probe on remainder
  // Probe on output1
  // Probe on output1

  // Notes on the sheet:
  //   input2: initial=0x2
  //   inupper: initial=0x3
  //   input1: initial=0x2
endmodule

module divideru4bit (
  input  [3:0] inupper,
  input  [3:0] input1,
  input  [3:0] input2,
  output [3:0] remainder,
  output [3:0] output1
);

  wire comparator_1_eq, comparator_2_eq, comparator_2_gt, comparator_3_eq, comparator_3_gt, comparator_4_eq,
       comparator_4_gt, comparator_5_eq, comparator_5_gt, comparator_6_eq, comparator_6_gt, comparator_7_eq,
       comparator_7_gt, comparator_8_eq, comparator_8_gt, comparator_9_eq, comparator_9_gt, not_1_out,
       or_1_out, or_2_out, or_3_out, or_4_out, or_5_out, or_6_out, or_7_out, or_8_out;
  wire [3:0] divider_1_out, divider_1_rem;
  wire [7:4] and_4_out;
  wire [15:0] cbuffer16bit_1_output1, cbuffer16bit_2_output1, cbuffer16bit_3_output1, cbuffer16bit_4_output1,
       cbuffer16bit_5_output1, cbuffer16bit_6_output1, cbuffer16bit_7_output1, cbuffer16bit_8_output1,
       subtractor16bit_1_output1, subtractor16bit_2_output1, subtractor16bit_3_output1,
       subtractor16bit_4_output1, subtractor16bit_5_output1, subtractor16bit_6_output1,
       subtractor16bit_7_output1;
  wire [15:4] subtractor16bit_8_output1;

  // Probe on inupper
  // Probe on inupper
  // Probe on input1
  // Probe on input1
  // Probe on input2
  // Probe on input2
  Comparator #(.mode("unsigned"), .width(4)) comparator_1 (
    .a(input2), .b(4'b0000), .eq(comparator_1_eq));  // open: gt, lt
  not not_1 (not_1_out, comparator_1_eq);
  Divider #(.width(4)) divider_1 (.a(input1), .b(input2), .out(divider_1_out), .upper(inupper), .rem(divider_1_rem));
  // Probe on divider_1_out
  // Probe on divider_1_out
  // Probe on divider_1_rem
  // Probe on divider_1_rem
  // Probe on {{8{1'b0}}, inupper, input1}
  // Probe on {{8{1'b0}}, inupper, input1}
  cbuffer16bit cbuffer16bit_1 (
    .buffer1(and_4_out[7]), .input1({{5{1'b0}}, input2, {7{1'b0}}}), .output1(cbuffer16bit_1_output1));
  and and_1 (and_4_out[7], or_1_out, not_1_out);
  or or_1 (or_1_out, comparator_2_gt, comparator_2_eq);
  Comparator #(.mode("unsigned"), .width(16)) comparator_2 (
    .a({{8{1'b0}}, inupper, input1}), .b({{5{1'b0}}, input2, {7{1'b0}}}), .gt(comparator_2_gt),
    .eq(comparator_2_eq));  // open: lt
  // Probe on subtractor16bit_1_output1
  // Probe on subtractor16bit_1_output1
  subtractor16bit subtractor16bit_1 (
    .input1({{8{1'b0}}, inupper, input1}), .input2(cbuffer16bit_1_output1),
    .output1(subtractor16bit_1_output1));  // open: inborrow, borrow
  cbuffer16bit cbuffer16bit_2 (
    .buffer1(and_4_out[6]), .input1({{6{1'b0}}, input2, {6{1'b0}}}), .output1(cbuffer16bit_2_output1));
  and and_2 (and_4_out[6], or_2_out, not_1_out);
  or or_2 (or_2_out, comparator_3_gt, comparator_3_eq);
  Comparator #(.mode("unsigned"), .width(16)) comparator_3 (
    .a(subtractor16bit_1_output1), .b({{6{1'b0}}, input2, {6{1'b0}}}), .gt(comparator_3_gt),
    .eq(comparator_3_eq));  // open: lt
  // Probe on subtractor16bit_2_output1
  // Probe on subtractor16bit_2_output1
  subtractor16bit subtractor16bit_2 (
    .input1(subtractor16bit_1_output1), .input2(cbuffer16bit_2_output1), .output1(subtractor16bit_2_output1));  // open: inborrow, borrow
  cbuffer16bit cbuffer16bit_3 (
    .buffer1(and_4_out[5]), .input1({{7{1'b0}}, input2, {5{1'b0}}}), .output1(cbuffer16bit_3_output1));
  and and_3 (and_4_out[5], or_3_out, not_1_out);
  or or_3 (or_3_out, comparator_4_gt, comparator_4_eq);
  Comparator #(.mode("unsigned"), .width(16)) comparator_4 (
    .a(subtractor16bit_2_output1), .b({{7{1'b0}}, input2, {5{1'b0}}}), .gt(comparator_4_gt),
    .eq(comparator_4_eq));  // open: lt
  // Probe on subtractor16bit_3_output1
  // Probe on subtractor16bit_3_output1
  subtractor16bit subtractor16bit_3 (
    .input1(subtractor16bit_2_output1), .input2(cbuffer16bit_3_output1), .output1(subtractor16bit_3_output1));  // open: inborrow, borrow
  Comparator #(.mode("unsigned"), .width(16)) comparator_5 (
    .a(subtractor16bit_3_output1), .b({{8{1'b0}}, input2, 4'b0000}), .gt(comparator_5_gt),
    .eq(comparator_5_eq));  // open: lt
  cbuffer16bit cbuffer16bit_4 (
    .buffer1(and_4_out[4]), .input1({{8{1'b0}}, input2, 4'b0000}), .output1(cbuffer16bit_4_output1));
  and and_4 (and_4_out[4], or_4_out, not_1_out);
  or or_4 (or_4_out, comparator_5_gt, comparator_5_eq);
  subtractor16bit subtractor16bit_4 (
    .input1(subtractor16bit_3_output1), .input2(cbuffer16bit_4_output1), .output1(subtractor16bit_4_output1));  // open: inborrow, borrow
  // Probe on subtractor16bit_4_output1
  // Probe on subtractor16bit_4_output1
  Comparator #(.mode("unsigned"), .width(16)) comparator_6 (
    .a(subtractor16bit_4_output1), .b({{9{1'b0}}, input2, 3'b000}), .gt(comparator_6_gt), .eq(comparator_6_eq));  // open: lt
  cbuffer16bit cbuffer16bit_5 (
    .buffer1(output1[3]), .input1({{9{1'b0}}, input2, 3'b000}), .output1(cbuffer16bit_5_output1));
  and and_5 (output1[3], or_5_out, not_1_out);
  or or_5 (or_5_out, comparator_6_gt, comparator_6_eq);
  subtractor16bit subtractor16bit_5 (
    .input1(subtractor16bit_4_output1), .input2(cbuffer16bit_5_output1), .output1(subtractor16bit_5_output1));  // open: inborrow, borrow
  // Probe on subtractor16bit_5_output1
  // Probe on subtractor16bit_5_output1
  or or_6 (or_6_out, comparator_7_gt, comparator_7_eq);
  Comparator #(.mode("unsigned"), .width(16)) comparator_7 (
    .a(subtractor16bit_5_output1), .b({{10{1'b0}}, input2, 2'b00}), .gt(comparator_7_gt), .eq(comparator_7_eq));  // open: lt
  cbuffer16bit cbuffer16bit_6 (
    .buffer1(output1[2]), .input1({{10{1'b0}}, input2, 2'b00}), .output1(cbuffer16bit_6_output1));
  and and_6 (output1[2], or_6_out, not_1_out);
  subtractor16bit subtractor16bit_6 (
    .input1(subtractor16bit_5_output1), .input2(cbuffer16bit_6_output1), .output1(subtractor16bit_6_output1));  // open: inborrow, borrow
  // Probe on subtractor16bit_6_output1
  // Probe on subtractor16bit_6_output1
  cbuffer16bit cbuffer16bit_7 (
    .buffer1(output1[1]), .input1({{11{1'b0}}, input2, 1'b0}), .output1(cbuffer16bit_7_output1));
  and and_7 (output1[1], or_7_out, not_1_out);
  or or_7 (or_7_out, comparator_8_gt, comparator_8_eq);
  Comparator #(.mode("unsigned"), .width(16)) comparator_8 (
    .a(subtractor16bit_6_output1), .b({{11{1'b0}}, input2, 1'b0}), .gt(comparator_8_gt), .eq(comparator_8_eq));  // open: lt
  subtractor16bit subtractor16bit_7 (
    .input1(subtractor16bit_6_output1), .input2(cbuffer16bit_7_output1), .output1(subtractor16bit_7_output1));  // open: inborrow, borrow
  // Probe on subtractor16bit_7_output1
  // Probe on subtractor16bit_7_output1
  cbuffer16bit cbuffer16bit_8 (.buffer1(output1[0]), .input1({{12{1'b0}}, input2}), .output1(cbuffer16bit_8_output1));
  and and_8 (output1[0], or_8_out, not_1_out);
  or or_8 (or_8_out, comparator_9_gt, comparator_9_eq);
  Comparator #(.mode("unsigned"), .width(16)) comparator_9 (
    .a(subtractor16bit_7_output1), .b({{12{1'b0}}, input2}), .gt(comparator_9_gt), .eq(comparator_9_eq));  // open: lt
  // Probe on {subtractor16bit_8_output1, remainder}
  // Probe on {subtractor16bit_8_output1, remainder}
  subtractor16bit subtractor16bit_8 (
    .input1(subtractor16bit_7_output1), .input2(cbuffer16bit_8_output1),
    .output1({subtractor16bit_8_output1, remainder}));  // open: inborrow, borrow
  // Probe on {{8{1'b0}}, and_4_out, output1}
  // Probe on {{8{1'b0}}, and_4_out, output1}
  // Probe on remainder
  // Probe on remainder
  // Probe on output1
  // Probe on output1
endmodule

module divideru8bit (
  input  [7:0] inupper,
  input  [7:0] input1,
  input  [7:0] input2,
  output [7:0] remainder,
  output [7:0] output1
);

  wire comparator_1_eq, comparator_2_eq, comparator_2_gt, comparator_3_eq, comparator_3_gt, comparator_4_eq,
       comparator_4_gt, comparator_5_eq, comparator_5_gt, comparator_6_eq, comparator_6_gt, comparator_7_eq,
       comparator_7_gt, comparator_8_eq, comparator_8_gt, comparator_9_eq, comparator_9_gt, comparator_10_eq,
       comparator_10_gt, comparator_11_eq, comparator_11_gt, comparator_12_eq, comparator_12_gt,
       comparator_13_eq, comparator_13_gt, comparator_14_eq, comparator_14_gt, comparator_15_eq,
       comparator_15_gt, comparator_16_eq, comparator_16_gt, comparator_17_eq, comparator_17_gt, not_1_out,
       or_1_out, or_2_out, or_3_out, or_4_out, or_5_out, or_6_out, or_7_out, or_8_out, or_9_out, or_10_out,
       or_11_out, or_12_out, or_13_out, or_14_out, or_15_out, or_16_out;
  wire [7:0] divider_1_out, divider_1_rem;
  wire [15:8] and_8_out;
  wire [31:0] cbuffer32bit_1_output1, cbuffer32bit_2_output1, cbuffer32bit_3_output1, cbuffer32bit_4_output1,
       cbuffer32bit_5_output1, cbuffer32bit_6_output1, cbuffer32bit_7_output1, cbuffer32bit_8_output1,
       cbuffer32bit_9_output1, cbuffer32bit_10_output1, cbuffer32bit_11_output1, cbuffer32bit_12_output1,
       cbuffer32bit_13_output1, cbuffer32bit_14_output1, cbuffer32bit_15_output1, cbuffer32bit_16_output1,
       subtractor32bit_1_output1, subtractor32bit_2_output1, subtractor32bit_3_output1,
       subtractor32bit_4_output1, subtractor32bit_5_output1, subtractor32bit_6_output1,
       subtractor32bit_7_output1, subtractor32bit_8_output1, subtractor32bit_9_output1,
       subtractor32bit_10_output1, subtractor32bit_11_output1, subtractor32bit_12_output1,
       subtractor32bit_13_output1, subtractor32bit_14_output1, subtractor32bit_15_output1;
  wire [31:8] subtractor32bit_16_output1;

  // Probe on divider_1_out
  // Probe on divider_1_out
  Divider divider_1 (.a(input1), .b(input2), .out(divider_1_out), .upper(inupper), .rem(divider_1_rem));
  // Probe on divider_1_rem
  // Probe on divider_1_rem
  // Probe on inupper
  // Probe on inupper
  // Probe on input1
  // Probe on input1
  // Probe on input2
  // Probe on input2
  not not_1 (not_1_out, comparator_1_eq);
  Comparator #(.mode("unsigned")) comparator_1 (.a(input2), .b({8{1'b0}}), .eq(comparator_1_eq));  // open: gt, lt
  // Probe on {{16{1'b0}}, inupper, input1}
  // Probe on {{16{1'b0}}, inupper, input1}
  subtractor32bit subtractor32bit_1 (
    .input1({{16{1'b0}}, inupper, input1}), .input2(cbuffer32bit_1_output1),
    .output1(subtractor32bit_1_output1));  // open: inborrow, borrow
  cbuffer32bit cbuffer32bit_1 (
    .buffer1(and_8_out[15]), .input1({{9{1'b0}}, input2, {15{1'b0}}}), .output1(cbuffer32bit_1_output1));
  and and_1 (and_8_out[15], or_1_out, not_1_out);
  or or_1 (or_1_out, comparator_2_gt, comparator_2_eq);
  Comparator #(.mode("unsigned"), .width(32)) comparator_2 (
    .a({{16{1'b0}}, inupper, input1}), .b({{9{1'b0}}, input2, {15{1'b0}}}), .gt(comparator_2_gt),
    .eq(comparator_2_eq));  // open: lt
  // Probe on subtractor32bit_1_output1
  // Probe on subtractor32bit_1_output1
  subtractor32bit subtractor32bit_2 (
    .input1(subtractor32bit_1_output1), .input2(cbuffer32bit_2_output1), .output1(subtractor32bit_2_output1));  // open: inborrow, borrow
  cbuffer32bit cbuffer32bit_2 (
    .buffer1(and_8_out[14]), .input1({{10{1'b0}}, input2, {14{1'b0}}}), .output1(cbuffer32bit_2_output1));
  and and_2 (and_8_out[14], or_2_out, not_1_out);
  or or_2 (or_2_out, comparator_3_gt, comparator_3_eq);
  Comparator #(.mode("unsigned"), .width(32)) comparator_3 (
    .a(subtractor32bit_1_output1), .b({{10{1'b0}}, input2, {14{1'b0}}}), .gt(comparator_3_gt),
    .eq(comparator_3_eq));  // open: lt
  // Probe on subtractor32bit_2_output1
  // Probe on subtractor32bit_2_output1
  subtractor32bit subtractor32bit_3 (
    .input1(subtractor32bit_2_output1), .input2(cbuffer32bit_3_output1), .output1(subtractor32bit_3_output1));  // open: inborrow, borrow
  cbuffer32bit cbuffer32bit_3 (
    .buffer1(and_8_out[13]), .input1({{11{1'b0}}, input2, {13{1'b0}}}), .output1(cbuffer32bit_3_output1));
  and and_3 (and_8_out[13], or_3_out, not_1_out);
  or or_3 (or_3_out, comparator_4_gt, comparator_4_eq);
  // Probe on subtractor32bit_3_output1
  // Probe on subtractor32bit_3_output1
  subtractor32bit subtractor32bit_4 (
    .input1(subtractor32bit_3_output1), .input2(cbuffer32bit_4_output1), .output1(subtractor32bit_4_output1));  // open: inborrow, borrow
  or or_4 (or_4_out, comparator_5_gt, comparator_5_eq);
  Comparator #(.mode("unsigned"), .width(32)) comparator_4 (
    .a(subtractor32bit_2_output1), .b({{11{1'b0}}, input2, {13{1'b0}}}), .gt(comparator_4_gt),
    .eq(comparator_4_eq));  // open: lt
  cbuffer32bit cbuffer32bit_4 (
    .buffer1(and_8_out[12]), .input1({{12{1'b0}}, input2, {12{1'b0}}}), .output1(cbuffer32bit_4_output1));
  and and_4 (and_8_out[12], or_4_out, not_1_out);
  Comparator #(.mode("unsigned"), .width(32)) comparator_5 (
    .a(subtractor32bit_3_output1), .b({{12{1'b0}}, input2, {12{1'b0}}}), .gt(comparator_5_gt),
    .eq(comparator_5_eq));  // open: lt
  // Probe on subtractor32bit_4_output1
  // Probe on subtractor32bit_4_output1
  subtractor32bit subtractor32bit_5 (
    .input1(subtractor32bit_4_output1), .input2(cbuffer32bit_5_output1), .output1(subtractor32bit_5_output1));  // open: inborrow, borrow
  cbuffer32bit cbuffer32bit_5 (
    .buffer1(and_8_out[11]), .input1({{13{1'b0}}, input2, {11{1'b0}}}), .output1(cbuffer32bit_5_output1));
  and and_5 (and_8_out[11], or_5_out, not_1_out);
  or or_5 (or_5_out, comparator_6_gt, comparator_6_eq);
  Comparator #(.mode("unsigned"), .width(32)) comparator_6 (
    .a(subtractor32bit_4_output1), .b({{13{1'b0}}, input2, {11{1'b0}}}), .gt(comparator_6_gt),
    .eq(comparator_6_eq));  // open: lt
  // Probe on subtractor32bit_5_output1
  // Probe on subtractor32bit_5_output1
  subtractor32bit subtractor32bit_6 (
    .input1(subtractor32bit_5_output1), .input2(cbuffer32bit_6_output1), .output1(subtractor32bit_6_output1));  // open: inborrow, borrow
  cbuffer32bit cbuffer32bit_6 (
    .buffer1(and_8_out[10]), .input1({{14{1'b0}}, input2, {10{1'b0}}}), .output1(cbuffer32bit_6_output1));
  and and_6 (and_8_out[10], or_6_out, not_1_out);
  or or_6 (or_6_out, comparator_7_gt, comparator_7_eq);
  Comparator #(.mode("unsigned"), .width(32)) comparator_7 (
    .a(subtractor32bit_5_output1), .b({{14{1'b0}}, input2, {10{1'b0}}}), .gt(comparator_7_gt),
    .eq(comparator_7_eq));  // open: lt
  // Probe on subtractor32bit_6_output1
  // Probe on subtractor32bit_6_output1
  subtractor32bit subtractor32bit_7 (
    .input1(subtractor32bit_6_output1), .input2(cbuffer32bit_7_output1), .output1(subtractor32bit_7_output1));  // open: inborrow, borrow
  cbuffer32bit cbuffer32bit_7 (
    .buffer1(and_8_out[9]), .input1({{15{1'b0}}, input2, {9{1'b0}}}), .output1(cbuffer32bit_7_output1));
  and and_7 (and_8_out[9], or_7_out, not_1_out);
  or or_7 (or_7_out, comparator_8_gt, comparator_8_eq);
  // Probe on subtractor32bit_7_output1
  // Probe on subtractor32bit_7_output1
  subtractor32bit subtractor32bit_8 (
    .input1(subtractor32bit_7_output1), .input2(cbuffer32bit_8_output1), .output1(subtractor32bit_8_output1));  // open: inborrow, borrow
  or or_8 (or_8_out, comparator_9_gt, comparator_9_eq);
  Comparator #(.mode("unsigned"), .width(32)) comparator_8 (
    .a(subtractor32bit_6_output1), .b({{15{1'b0}}, input2, {9{1'b0}}}), .gt(comparator_8_gt),
    .eq(comparator_8_eq));  // open: lt
  cbuffer32bit cbuffer32bit_8 (
    .buffer1(and_8_out[8]), .input1({{16{1'b0}}, input2, {8{1'b0}}}), .output1(cbuffer32bit_8_output1));
  and and_8 (and_8_out[8], or_8_out, not_1_out);
  Comparator #(.mode("unsigned"), .width(32)) comparator_9 (
    .a(subtractor32bit_7_output1), .b({{16{1'b0}}, input2, {8{1'b0}}}), .gt(comparator_9_gt),
    .eq(comparator_9_eq));  // open: lt
  // Probe on subtractor32bit_8_output1
  // Probe on subtractor32bit_8_output1
  subtractor32bit subtractor32bit_9 (
    .input1(subtractor32bit_8_output1), .input2(cbuffer32bit_9_output1), .output1(subtractor32bit_9_output1));  // open: inborrow, borrow
  cbuffer32bit cbuffer32bit_9 (
    .buffer1(output1[7]), .input1({{17{1'b0}}, input2, {7{1'b0}}}), .output1(cbuffer32bit_9_output1));
  and and_9 (output1[7], or_9_out, not_1_out);
  or or_9 (or_9_out, comparator_10_gt, comparator_10_eq);
  Comparator #(.mode("unsigned"), .width(32)) comparator_10 (
    .a(subtractor32bit_8_output1), .b({{17{1'b0}}, input2, {7{1'b0}}}), .gt(comparator_10_gt),
    .eq(comparator_10_eq));  // open: lt
  // Probe on subtractor32bit_9_output1
  // Probe on subtractor32bit_9_output1
  subtractor32bit subtractor32bit_10 (
    .input1(subtractor32bit_9_output1), .input2(cbuffer32bit_10_output1), .output1(subtractor32bit_10_output1));  // open: inborrow, borrow
  cbuffer32bit cbuffer32bit_10 (
    .buffer1(output1[6]), .input1({{18{1'b0}}, input2, {6{1'b0}}}), .output1(cbuffer32bit_10_output1));
  and and_10 (output1[6], or_10_out, not_1_out);
  or or_10 (or_10_out, comparator_11_gt, comparator_11_eq);
  Comparator #(.mode("unsigned"), .width(32)) comparator_11 (
    .a(subtractor32bit_9_output1), .b({{18{1'b0}}, input2, {6{1'b0}}}), .gt(comparator_11_gt),
    .eq(comparator_11_eq));  // open: lt
  // Probe on subtractor32bit_10_output1
  // Probe on subtractor32bit_10_output1
  subtractor32bit subtractor32bit_11 (
    .input1(subtractor32bit_10_output1), .input2(cbuffer32bit_11_output1),
    .output1(subtractor32bit_11_output1));  // open: inborrow, borrow
  cbuffer32bit cbuffer32bit_11 (
    .buffer1(output1[5]), .input1({{19{1'b0}}, input2, {5{1'b0}}}), .output1(cbuffer32bit_11_output1));
  and and_11 (output1[5], or_11_out, not_1_out);
  or or_11 (or_11_out, comparator_12_gt, comparator_12_eq);
  // Probe on subtractor32bit_11_output1
  // Probe on subtractor32bit_11_output1
  subtractor32bit subtractor32bit_12 (
    .input1(subtractor32bit_11_output1), .input2(cbuffer32bit_12_output1),
    .output1(subtractor32bit_12_output1));  // open: inborrow, borrow
  or or_12 (or_12_out, comparator_13_gt, comparator_13_eq);
  Comparator #(.mode("unsigned"), .width(32)) comparator_12 (
    .a(subtractor32bit_10_output1), .b({{19{1'b0}}, input2, {5{1'b0}}}), .gt(comparator_12_gt),
    .eq(comparator_12_eq));  // open: lt
  cbuffer32bit cbuffer32bit_12 (
    .buffer1(output1[4]), .input1({{20{1'b0}}, input2, 4'b0000}), .output1(cbuffer32bit_12_output1));
  and and_12 (output1[4], or_12_out, not_1_out);
  Comparator #(.mode("unsigned"), .width(32)) comparator_13 (
    .a(subtractor32bit_11_output1), .b({{20{1'b0}}, input2, 4'b0000}), .gt(comparator_13_gt),
    .eq(comparator_13_eq));  // open: lt
  // Probe on subtractor32bit_12_output1
  // Probe on subtractor32bit_12_output1
  subtractor32bit subtractor32bit_13 (
    .input1(subtractor32bit_12_output1), .input2(cbuffer32bit_13_output1),
    .output1(subtractor32bit_13_output1));  // open: inborrow, borrow
  cbuffer32bit cbuffer32bit_13 (
    .buffer1(output1[3]), .input1({{21{1'b0}}, input2, 3'b000}), .output1(cbuffer32bit_13_output1));
  and and_13 (output1[3], or_13_out, not_1_out);
  or or_13 (or_13_out, comparator_14_gt, comparator_14_eq);
  Comparator #(.mode("unsigned"), .width(32)) comparator_14 (
    .a(subtractor32bit_12_output1), .b({{21{1'b0}}, input2, 3'b000}), .gt(comparator_14_gt),
    .eq(comparator_14_eq));  // open: lt
  // Probe on subtractor32bit_13_output1
  // Probe on subtractor32bit_13_output1
  subtractor32bit subtractor32bit_14 (
    .input1(subtractor32bit_13_output1), .input2(cbuffer32bit_14_output1),
    .output1(subtractor32bit_14_output1));  // open: inborrow, borrow
  cbuffer32bit cbuffer32bit_14 (
    .buffer1(output1[2]), .input1({{22{1'b0}}, input2, 2'b00}), .output1(cbuffer32bit_14_output1));
  and and_14 (output1[2], or_14_out, not_1_out);
  or or_14 (or_14_out, comparator_15_gt, comparator_15_eq);
  Comparator #(.mode("unsigned"), .width(32)) comparator_15 (
    .a(subtractor32bit_13_output1), .b({{22{1'b0}}, input2, 2'b00}), .gt(comparator_15_gt),
    .eq(comparator_15_eq));  // open: lt
  // Probe on subtractor32bit_14_output1
  // Probe on subtractor32bit_14_output1
  subtractor32bit subtractor32bit_15 (
    .input1(subtractor32bit_14_output1), .input2(cbuffer32bit_15_output1),
    .output1(subtractor32bit_15_output1));  // open: inborrow, borrow
  cbuffer32bit cbuffer32bit_15 (
    .buffer1(output1[1]), .input1({{23{1'b0}}, input2, 1'b0}), .output1(cbuffer32bit_15_output1));
  and and_15 (output1[1], or_15_out, not_1_out);
  or or_15 (or_15_out, comparator_16_gt, comparator_16_eq);
  // Probe on subtractor32bit_15_output1
  // Probe on subtractor32bit_15_output1
  subtractor32bit subtractor32bit_16 (
    .input1(subtractor32bit_15_output1), .input2(cbuffer32bit_16_output1),
    .output1({subtractor32bit_16_output1, remainder}));  // open: inborrow, borrow
  or or_16 (or_16_out, comparator_17_gt, comparator_17_eq);
  Comparator #(.mode("unsigned"), .width(32)) comparator_16 (
    .a(subtractor32bit_14_output1), .b({{23{1'b0}}, input2, 1'b0}), .gt(comparator_16_gt),
    .eq(comparator_16_eq));  // open: lt
  cbuffer32bit cbuffer32bit_16 (.buffer1(output1[0]), .input1({{24{1'b0}}, input2}), .output1(cbuffer32bit_16_output1));
  and and_16 (output1[0], or_16_out, not_1_out);
  Comparator #(.mode("unsigned"), .width(32)) comparator_17 (
    .a(subtractor32bit_15_output1), .b({{24{1'b0}}, input2}), .gt(comparator_17_gt), .eq(comparator_17_eq));  // open: lt
  // Probe on {subtractor32bit_16_output1, remainder}
  // Probe on {subtractor32bit_16_output1, remainder}
  // Probe on {{16{1'b0}}, and_8_out, output1}
  // Probe on {{16{1'b0}}, and_8_out, output1}
  // Probe on remainder
  // Probe on remainder
  // Probe on output1
  // Probe on output1

  // Notes on the sheet:
  //   input2: initial=0x13
  //   input1: initial=0x4e
endmodule
