// Logisim project fpcomp.circ as structural Verilog
module fneg64 (
  input  [63:0] inval1,
  output [63:0] outval1
);

  // Probe on inval1
  not not_1 (outval1[63], inval1[63]);
  // Probe on {outval1[63], inval1[62:0]}

  assign outval1[62:0] = inval1[62:0];

  // Notes on the sheet:
  //   inval1: initial=0x4040152bd3c36113
endmodule

module fadd64 (
  input  [63:0] inval1,
  input  [63:0] inval2,
  output [63:0] outval1
);
endmodule

module fsub64 (
  input  [63:0] inval1,
  input  [63:0] inval2,
  output [63:0] outval1
);
endmodule

module fmul64 (
  input  [63:0] inval1,
  input  [63:0] inval2,
  output [63:0] outval1
);
endmodule

module fdiv64 (
  input  [63:0] inval1,
  input  [63:0] inval2,
  output [63:0] outval1
);
endmodule
