// Logisim project microfpgamux.circ as structural Verilog: 2 circuits, main circuit core
module core (
);

  wire adder_1_cout, and_1_out, and_3_out, and_4_out, and_5_out, bitselector_9_out, bitselector_10_out,
       bitselector_14_out, clock_1_out, clock_3_out, clock_6_out, comparator_1_eq, comparator_2_eq,
       comparator_3_eq, comparator_4_eq, comparator_5_eq, comparator_6_eq, comparator_6_lt, comparator_7_eq,
       comparator_8_eq, comparator_9_eq, comparator_10_eq, comparator_10_gt, comparator_10_lt,
       fpcomparator_1_p3, fpcomparator_1_p4, multiplexer_1_out, multiplexer_5_out, not_1_out, not_6_out,
       or_2_out, ram1_p4, regX_p3, regX_p4, regY_p4, regZ_p4, subtractor_1_bout;
  wire [1:0] bitselector_15_out;
  wire [3:0] bitselector_6_out, bitselector_7_out;
  wire [5:0] bitselector_8_out, bitselector_11_out, bitselector_12_out, bitselector_13_out;
  wire [7:0] bitselector_5_out;
  wire [15:0] bitselector_1_out, bitselector_2_out, bitselector_3_out, bitselector_4_out;
  wire [23:0] bitselector_16_out, bitselector_17_out, counter_2_q;
  wire [31:0] counter_1_q;
  wire [63:0] adder_1_out, and_2_out, and_6_out, and_7_out, and_8_out, bit_extender_1_out,
       bit_extender_2_out, buffer_1_out, divider_1_out, divider_1_rem, fpadder_1_out, fpcomparator_1_p1,
       fpdivider_1_out, fpmultiplier_1_out, fpnegator_1_p2, fpsubtractor_1_out, fptoint_1_p1, fptoint_2_p1,
       fptoint_3_p1, fptoint_4_p1, inttofp_1_p1, multiplexer_2_out, multiplexer_3_out, multiplexer_4_out,
       multiplexer_6_out, multiplier_1_cout, multiplier_1_out, nand_1_out, negator_1_out, nor_1_out,
       not_2_out, not_3_out, not_4_out, not_5_out, or_1_out, or_3_out, or_4_out, or_5_out, ram1_p6, ram1_p7,
       register_1_q, regX_p5, regX_p6, regZ_p6, shifter_1_out, shifter_2_out, shifter_3_out, shifter_4_out,
       shifter_5_out, shifter_6_out, shifter_7_out, shifter_8_out, subtractor_1_out, xnor_1_out, xor_1_out;

  BitSelector #(.group(16), .width(64)) bitselector_1 (.in(register_1_q), .out(bitselector_1_out), .sel(2'b11));
  BitSelector #(.group(16), .width(64)) bitselector_2 (.in(register_1_q), .out(bitselector_2_out), .sel(2'b10));
  BitSelector #(.group(16), .width(64)) bitselector_3 (.in(register_1_q), .out(bitselector_3_out), .sel(2'b01));
  BitSelector #(.group(16), .width(64)) bitselector_4 (.in(register_1_q), .out(bitselector_4_out), .sel(2'b00));
  Register #(.trigger("falling"), .width(64)) register_1 (
    .D(ram1_p6), .en(1'b1), .clk(clock_1_out), .Q(register_1_q));  // open: clr
  Clock clock_1 (.out(clock_1_out));
  BitSelector #(.group(8), .width(16)) bitselector_5 (.in(bitselector_4_out), .out(bitselector_5_out), .sel(1'b1));
  BitSelector #(.group(4), .width(16)) bitselector_6 (.in(bitselector_4_out), .out(bitselector_6_out), .sel(2'b01));
  BitSelector #(.group(4), .width(16)) bitselector_7 (.in(bitselector_4_out), .out(bitselector_7_out), .sel(2'b00));
  // DualRAM #(.addrWidth(16), .dataWidth(64), .enables("line")) regX: pin names not known; wires that end beside it: bitselector_1_out, bitselector_1_out, regX_p3, regX_p4, regX_p5, regX_p6
  Clock clock_2 (.out(regX_p4));
  BitSelector #(.group(6)) bitselector_8 (.in(bitselector_5_out), .out(bitselector_8_out), .sel(1'b0));
  BitSelector #(.width(4)) bitselector_9 (.in(bitselector_6_out), .out(bitselector_9_out), .sel(2'b00));
  BitSelector #(.width(4)) bitselector_10 (.in(bitselector_6_out), .out(bitselector_10_out), .sel(2'b00));
  BitSelector #(.group(6)) bitselector_11 (.in(bitselector_5_out), .out(bitselector_11_out), .sel(1'b0));
  BitSelector #(.group(6)) bitselector_12 (.in(bitselector_5_out), .out(bitselector_12_out), .sel(1'b0));
  BitSelector #(.group(6), .width(64)) bitselector_13 (.in(regZ_p6), .out(bitselector_13_out), .sel(4'b0000));
  Comparator #(.mode("unsigned"), .width(4)) comparator_1 (
    .a(bitselector_7_out), .b(4'b0000), .eq(comparator_1_eq));  // open: gt, lt
  Counter #(.max('hffffffff), .trigger("falling"), .width(32)) counter_1 (
    .load(or_2_out), .D({32{1'b0}}), .count(comparator_1_eq), .Q(counter_1_q), .clk(clock_3_out));  // open: carry, up, clr
  Clock clock_3 (.out(clock_3_out));
  BitSelector #(.width(64)) bitselector_14 (.in(fpcomparator_1_p1), .out(bitselector_14_out), .sel(bitselector_8_out));
  Comparator #(.mode("unsigned"), .width(4)) comparator_2 (
    .a(bitselector_7_out), .b(4'b0001), .eq(comparator_2_eq));  // open: gt, lt
  Comparator #(.mode("unsigned"), .width(4)) comparator_3 (
    .a(bitselector_7_out), .b(4'b0010), .eq(comparator_3_eq));  // open: gt, lt
  Comparator #(.mode("unsigned"), .width(4)) comparator_4 (
    .a(bitselector_7_out), .b(4'b0011), .eq(comparator_4_eq));  // open: gt, lt
  and and_1 (and_1_out, comparator_4_eq, bitselector_10_out);
  not not_1 (not_1_out, bitselector_10_out);
  Comparator #(.mode("unsigned"), .width(4)) comparator_5 (
    .a(bitselector_7_out), .b(4'b0100), .eq(comparator_5_eq));  // open: gt, lt
  BitSelector #(.group(2), .width(4)) bitselector_15 (.in(bitselector_6_out), .out(bitselector_15_out), .sel(1'b0));
  Comparator #(.width(64)) comparator_6 (
    .a(fpcomparator_1_p1), .b({64{1'b0}}), .eq(comparator_6_eq), .lt(comparator_6_lt));  // open: gt
  // FPComparator #(.fpwidth(64)) fpcomparator_1: pin names not known; wires that end beside it: fpcomparator_1_p1, {64{1'b0}}, fpcomparator_1_p3, fpcomparator_1_p4
  Comparator #(.mode("unsigned"), .width(4)) comparator_7 (
    .a(bitselector_7_out), .b(4'b0101), .eq(comparator_7_eq));  // open: gt, lt
  assign and_2_out = regX_p6 & not_2_out;  // AND_Gate and_2, 64 bits wide
  Adder #(.width(64)) adder_1 (
    .a(regZ_p6), .b(fpcomparator_1_p1), .out(adder_1_out), .cout(adder_1_cout));  // open: cin
  assign not_2_out = ~shifter_3_out;  // NOT_Gate not_2, 64 bits wide
  assign bit_extender_1_out = {{63{1'b0}}, adder_1_cout};  // Bit_Extender bit_extender_1
  Comparator #(.mode("unsigned"), .width(4)) comparator_8 (
    .a(bitselector_7_out), .b(4'b0110), .eq(comparator_8_eq));  // open: gt, lt
  Shifter #(.width(64)) shifter_1 (.in(fpcomparator_1_p1), .\dist (bitselector_13_out), .out(shifter_1_out));
  Comparator #(.mode("unsigned"), .width(4)) comparator_9 (
    .a(bitselector_7_out), .b(4'b0111), .eq(comparator_9_eq));  // open: gt, lt
  FPAdder #(.fpwidth(64)) fpadder_1 (.a(fpcomparator_1_p1), .b(regZ_p6), .out(fpadder_1_out));
  Comparator #(.mode("unsigned"), .width(32)) comparator_10 (
    .a(counter_1_q), .b({bitselector_2_out, bitselector_3_out}), .gt(comparator_10_gt),
    .eq(comparator_10_eq), .lt(comparator_10_lt));
  and and_3 (and_3_out, not_1_out, comparator_4_eq);
  assign not_3_out = ~shifter_2_out;  // NOT_Gate not_3, 64 bits wide
  Multiplexer #(.select(2)) multiplexer_1 (
    .in0(comparator_6_eq), .in1(comparator_6_lt), .in2(fpcomparator_1_p3), .in3(fpcomparator_1_p4),
    .out(multiplexer_1_out), .sel(bitselector_15_out));
  Shifter #(.width(64)) shifter_2 (.in(64'h1), .\dist (bitselector_11_out), .out(shifter_2_out));
  Multiplexer #(.select(4), .width(64)) multiplexer_2 (
    .in0(adder_1_out), .in1(or_1_out), .in2(subtractor_1_out), .in3(or_4_out), .in4(multiplier_1_out),
    .in5(multiplier_1_cout), .in6(divider_1_out), .in7(divider_1_rem), .in8(negator_1_out),
    .out(multiplexer_2_out), .sel(bitselector_6_out));  // open: in9, in10, in11, in12, in13, in14, in15
  assign or_1_out = and_2_out | shifter_3_out;  // OR_Gate or_1, 64 bits wide
  Shifter #(.width(64)) shifter_3 (.in(bit_extender_1_out), .\dist (bitselector_12_out), .out(shifter_3_out));
  Multiplexer #(.select(4), .width(64)) multiplexer_3 (
    .in0(shifter_1_out), .in1(shifter_4_out), .in2(shifter_5_out), .in3(shifter_7_out), .in4(shifter_8_out),
    .in5(buffer_1_out), .in6(not_5_out), .in7(or_5_out), .in8(and_8_out), .in9(nand_1_out), .in10(nor_1_out),
    .in11(xor_1_out), .in12(xnor_1_out), .out(multiplexer_3_out), .sel(bitselector_6_out));  // open: in13, in14, in15
  Shifter #(.shift("lr"), .width(64)) shifter_4 (
    .in(fpcomparator_1_p1), .\dist (bitselector_13_out), .out(shifter_4_out));
  Multiplexer #(.select(4), .width(64)) multiplexer_4 (
    .in0(fpadder_1_out), .in1(fpsubtractor_1_out), .in2(fpmultiplier_1_out), .in3(fpdivider_1_out),
    .in4(fpnegator_1_p2), .in5(inttofp_1_p1), .in6(fptoint_1_p1), .in7(fptoint_2_p1), .in8(fptoint_3_p1),
    .in9(fptoint_4_p1), .out(multiplexer_4_out), .sel(bitselector_6_out));  // open: in10, in11, in12, in13, in14, in15
  FPSubtractor #(.fpwidth(64)) fpsubtractor_1 (.a(fpcomparator_1_p1), .b(regZ_p6), .out(fpsubtractor_1_out));
  or or_2 (or_2_out, comparator_10_gt, comparator_10_eq);
  and and_4 (and_4_out, comparator_10_lt, comparator_1_eq);
  and and_5 (and_5_out, bitselector_14_out, comparator_2_eq);
  assign and_6_out = regX_p6 & not_3_out;  // AND_Gate and_6, 64 bits wide
  assign or_3_out = and_6_out | shifter_2_out;  // OR_Gate or_3, 64 bits wide
  Subtractor #(.width(64)) subtractor_1 (
    .a(fpcomparator_1_p1), .b(regZ_p6), .out(subtractor_1_out), .bout(subtractor_1_bout));  // open: bin
  Shifter #(.shift("ar"), .width(64)) shifter_5 (
    .in(fpcomparator_1_p1), .\dist (bitselector_13_out), .out(shifter_5_out));
  FPMultiplier #(.fpwidth(64)) fpmultiplier_1 (.a(fpcomparator_1_p1), .b(regZ_p6), .out(fpmultiplier_1_out));
  Multiplexer multiplexer_5 (.in0(and_5_out), .in1(comparator_2_eq), .out(multiplexer_5_out), .sel(bitselector_9_out));
  Multiplexer #(.width(64)) multiplexer_6 (
    .in0(and_6_out), .in1(or_3_out), .out(multiplexer_6_out), .sel(multiplexer_1_out));
  assign and_7_out = regX_p6 & not_4_out;  // AND_Gate and_7, 64 bits wide
  assign not_4_out = ~shifter_6_out;  // NOT_Gate not_4, 64 bits wide
  assign bit_extender_2_out = {{63{1'b0}}, subtractor_1_bout};  // Bit_Extender bit_extender_2
  Shifter #(.width(64)) shifter_6 (.in(bit_extender_2_out), .\dist (bitselector_12_out), .out(shifter_6_out));
  Shifter #(.shift("rl"), .width(64)) shifter_7 (
    .in(fpcomparator_1_p1), .\dist (bitselector_13_out), .out(shifter_7_out));
  FPDivider #(.fpwidth(64)) fpdivider_1 (.a(fpcomparator_1_p1), .b(regZ_p6), .out(fpdivider_1_out));
  assign or_4_out = and_7_out | shifter_6_out;  // OR_Gate or_4, 64 bits wide
  assign not_5_out = ~fpcomparator_1_p1;  // NOT_Gate not_5, 64 bits wide
  assign or_5_out = fpcomparator_1_p1 | regZ_p6;  // OR_Gate or_5, 64 bits wide
  assign buffer_1_out = fpcomparator_1_p1;  // Buffer buffer_1, 64 bits wide
  Shifter #(.shift("rr"), .width(64)) shifter_8 (
    .in(fpcomparator_1_p1), .\dist (bitselector_13_out), .out(shifter_8_out));
  // FPNegator #(.fpwidth(64)) fpnegator_1: pin names not known; wires that end beside it: fpcomparator_1_p1, fpnegator_1_p2, fpcomparator_1_p1
  // IntToFP #(.fpwidth(64), .width(64)) inttofp_1: pin names not known; wires that end beside it: inttofp_1_p1, fpcomparator_1_p1
  Multiplier #(.width(64)) multiplier_1 (
    .a(fpcomparator_1_p1), .b(regZ_p6), .out(multiplier_1_out), .cout(multiplier_1_cout));  // open: cin
  assign nand_1_out = ~(fpcomparator_1_p1 & regZ_p6);  // NAND_Gate nand_1, 64 bits wide
  assign nor_1_out = ~(fpcomparator_1_p1 | regZ_p6);  // NOR_Gate nor_1, 64 bits wide
  assign and_8_out = fpcomparator_1_p1 & regZ_p6;  // AND_Gate and_8, 64 bits wide
  // FPToInt #(.fpwidth(64), .width(64)) fptoint_1: pin names not known; wires that end beside it: fptoint_1_p1, fpcomparator_1_p1
  Divider #(.mode("twosComplement"), .width(64)) divider_1 (
    .a(fpcomparator_1_p1), .b(regZ_p6), .out(divider_1_out), .rem(divider_1_rem));  // open: upper
  assign xnor_1_out = ~(fpcomparator_1_p1 ^ regZ_p6);  // XNOR_Gate xnor_1, 64 bits wide
  assign xor_1_out = fpcomparator_1_p1 ^ regZ_p6;  // XOR_Gate xor_1, 64 bits wide
  // FPToInt #(.fpwidth(64), .mode("floor"), .width(64)) fptoint_2: pin names not known; wires that end beside it: fptoint_2_p1, fpcomparator_1_p1
  Negator #(.width(64)) negator_1 (.in(fpcomparator_1_p1), .out(negator_1_out));
  // FPToInt #(.fpwidth(64), .mode("ceil"), .width(64)) fptoint_3: pin names not known; wires that end beside it: fptoint_3_p1, fpcomparator_1_p1
  // FPToInt #(.fpwidth(64), .mode("truncate"), .width(64)) fptoint_4: pin names not known; wires that end beside it: fptoint_4_p1
  // DualRAM #(.addrWidth(16), .dataWidth(64), .enables("line")) regY: pin names not known; wires that end beside it: bitselector_2_out, bitselector_1_out, regX_p3, regY_p4, regX_p5, fpcomparator_1_p1
  Clock clock_4 (.out(regY_p4));
  or or_6 (regX_p3, comparator_3_eq, and_3_out, comparator_5_eq, comparator_7_eq, comparator_8_eq, comparator_9_eq);
  Multiplexer #(.select(4), .width(64)) multiplexer_7 (
    .in0(ram1_p6), .in1(ram1_p6), .in2({{32{1'b0}}, bitselector_2_out, bitselector_3_out}), .in3(ram1_p7),
    .in4(multiplexer_6_out), .in5(multiplexer_2_out), .in6(multiplexer_3_out), .in7(multiplexer_4_out),
    .out(regX_p5), .sel(bitselector_7_out));  // open: in8, in9, in10, in11, in12, in13, in14, in15
  BitSelector #(.group(24), .width(64)) bitselector_16 (.in(regX_p6), .out(bitselector_16_out), .sel(2'b00));
  BitSelector #(.group(24), .width(64)) bitselector_17 (.in(fpcomparator_1_p1), .out(bitselector_17_out), .sel(2'b00));
  // DualRAM #(.addrWidth(16), .dataWidth(64), .enables("line")) regZ: pin names not known; wires that end beside it: bitselector_3_out, bitselector_1_out, regX_p3, regZ_p4, regX_p5, regZ_p6
  Clock clock_5 (.out(regZ_p4));
  Counter #(.max('hffffff), .width(24)) counter_2 (
    .load(multiplexer_5_out), .D(bitselector_16_out), .count(not_6_out), .Q(counter_2_q), .clk(clock_6_out));  // open: carry, up, clr
  not not_6 (not_6_out, and_4_out);
  Clock clock_6 (.out(clock_6_out));
  // DualRAM #(.addrWidth(24), .dataWidth(64), .enables("line"), .\type ("nonvolatile")) ram1: pin names not known; wires that end beside it: counter_2_q, bitselector_17_out, and_1_out, ram1_p4, regX_p6, ram1_p6, ram1_p7
  Clock clock_7 (.out(ram1_p4));
  muxreg muxreg_1 ();  // open: IN0, IN1, IN2, IN3, IN4, IN5, IN6, IN7, IN8, IN9, IN10, IN11, IN12, IN13, IN14, IN15, A0, A1, A2, A3, A4, A5, A6, A7, A8, A9, A10, A11, A12, A13, A14, A15, LE0, LE1, LE2, LE3, LE4, LE5, LE6, LE7, LE8, LE9, LE10, LE11, LE12, LE13, LE14, LE15, DA0, DB0, DA1, DB1, DA2, DB2, DA3, DB3, DA4, DB4, DA5, DB5, DA6, DB6, DA7, DB7, DA8, DB8, DA9, DB9, DA10, DB10, DA11, DB11, DA12, DB12, DA13, DB13, DA14, DB14, DA15, DB15, OUTA0, OUTB0, OUTA1, OUTB1, OUTA2, OUTB2, OUTA3, OUTB3, OUTA4, OUTB4, OUTA5, OUTB5, OUTA6, OUTB6, OUTA7, OUTB7, OUTA8, OUTB8, OUTA9, OUTB9, OUTA10, OUTB10, OUTA11, OUTB11, OUTA12, OUTB12, OUTA13, OUTB13, OUTA14, OUTB14, OUTA15, OUTB15
endmodule

module muxreg (
  input  [63:0] IN0,
  input  [63:0] IN1,
  input  [63:0] IN2,
  input  [63:0] IN3,
  input  [63:0] IN4,
  input  [63:0] IN5,
  input  [63:0] IN6,
  input  [63:0] IN7,
  input  [63:0] IN8,
  input  [63:0] IN9,
  input  [63:0] IN10,
  input  [63:0] IN11,
  input  [63:0] IN12,
  input  [63:0] IN13,
  input  [63:0] IN14,
  input  [63:0] IN15,
  input  [3:0] A0,
  input  [3:0] A1,
  input  [3:0] A2,
  input  [3:0] A3,
  input  [3:0] A4,
  input  [3:0] A5,
  input  [3:0] A6,
  input  [3:0] A7,
  input  [3:0] A8,
  input  [3:0] A9,
  input  [3:0] A10,
  input  [3:0] A11,
  input  [3:0] A12,
  input  [3:0] A13,
  input  [3:0] A14,
  input  [3:0] A15,
  input  LE0,
  input  LE1,
  input  LE2,
  input  LE3,
  input  LE4,
  input  LE5,
  input  LE6,
  input  LE7,
  input  LE8,
  input  LE9,
  input  LE10,
  input  LE11,
  input  LE12,
  input  LE13,
  input  LE14,
  input  LE15,
  input  [3:0] DA0,
  input  [3:0] DB0,
  input  [3:0] DA1,
  input  [3:0] DB1,
  input  [3:0] DA2,
  input  [3:0] DB2,
  input  [3:0] DA3,
  input  [3:0] DB3,
  input  [3:0] DA4,
  input  [3:0] DB4,
  input  [3:0] DA5,
  input  [3:0] DB5,
  input  [3:0] DA6,
  input  [3:0] DB6,
  input  [3:0] DA7,
  input  [3:0] DB7,
  input  [3:0] DA8,
  input  [3:0] DB8,
  input  [3:0] DA9,
  input  [3:0] DB9,
  input  [3:0] DA10,
  input  [3:0] DB10,
  input  [3:0] DA11,
  input  [3:0] DB11,
  input  [3:0] DA12,
  input  [3:0] DB12,
  input  [3:0] DA13,
  input  [3:0] DB13,
  input  [3:0] DA14,
  input  [3:0] DB14,
  input  [3:0] DA15,
  input  [3:0] DB15,
  output [63:0] OUTA0,
  output [63:0] OUTB0,
  output [63:0] OUTA1,
  output [63:0] OUTB1,
  output [63:0] OUTA2,
  output [63:0] OUTB2,
  output [63:0] OUTA3,
  output [63:0] OUTB3,
  output [63:0] OUTA4,
  output [63:0] OUTB4,
  output [63:0] OUTA5,
  output [63:0] OUTB5,
  output [63:0] OUTA6,
  output [63:0] OUTB6,
  output [63:0] OUTA7,
  output [63:0] OUTB7,
  output [63:0] OUTA8,
  output [63:0] OUTB8,
  output [63:0] OUTA9,
  output [63:0] OUTB9,
  output [63:0] OUTA10,
  output [63:0] OUTB10,
  output [63:0] OUTA11,
  output [63:0] OUTB11,
  output [63:0] OUTA12,
  output [63:0] OUTB12,
  output [63:0] OUTA13,
  output [63:0] OUTB13,
  output [63:0] OUTA14,
  output [63:0] OUTB14,
  output [63:0] OUTA15,
  output [63:0] OUTB15
);

  wire clock_1_out, clock_2_out, clock_3_out, clock_4_out, clock_5_out, clock_6_out, clock_7_out,
       clock_8_out, clock_9_out, clock_10_out, clock_11_out, clock_12_out, clock_13_out, clock_14_out,
       clock_15_out, clock_16_out;
  wire [63:0] multiplexer_17_out, multiplexer_18_out, multiplexer_19_out, multiplexer_20_out,
       multiplexer_21_out, multiplexer_22_out, multiplexer_23_out, multiplexer_24_out, multiplexer_25_out,
       multiplexer_26_out, multiplexer_27_out, multiplexer_28_out, multiplexer_29_out, multiplexer_30_out,
       multiplexer_31_out, multiplexer_32_out, register_1_q, register_2_q, register_3_q, register_4_q,
       register_5_q, register_6_q, register_7_q, register_8_q, register_9_q, register_10_q, register_11_q,
       register_12_q, register_13_q, register_14_q, register_15_q, register_16_q;

  Multiplexer #(.select(4), .width(64)) multiplexer_1 (
    .in0(register_1_q), .in1(register_2_q), .in2(register_3_q), .in3(register_4_q), .in4(register_5_q),
    .in5(register_6_q), .in6(register_7_q), .in7(register_8_q), .in8(register_9_q), .in9(register_10_q),
    .in10(register_11_q), .in11(register_12_q), .in12(register_13_q), .in13(register_14_q),
    .in14(register_15_q), .in15(register_16_q), .out(OUTA0), .sel(DA0));
  Multiplexer #(.select(4), .width(64)) multiplexer_2 (
    .in0(register_1_q), .in1(register_2_q), .in2(register_3_q), .in3(register_4_q), .in4(register_5_q),
    .in5(register_6_q), .in6(register_7_q), .in7(register_8_q), .in8(register_9_q), .in9(register_10_q),
    .in10(register_11_q), .in11(register_12_q), .in12(register_13_q), .in13(register_14_q),
    .in14(register_15_q), .in15(register_16_q), .out(OUTA1), .sel(DA1));
  Multiplexer #(.select(4), .width(64)) multiplexer_3 (
    .in0(register_1_q), .in1(register_2_q), .in2(register_3_q), .in3(register_4_q), .in4(register_5_q),
    .in5(register_6_q), .in6(register_7_q), .in7(register_8_q), .in8(register_9_q), .in9(register_10_q),
    .in10(register_11_q), .in11(register_12_q), .in12(register_13_q), .in13(register_14_q),
    .in14(register_15_q), .in15(register_16_q), .out(OUTA2), .sel(DA2));
  Multiplexer #(.select(4), .width(64)) multiplexer_4 (
    .in0(register_1_q), .in1(register_2_q), .in2(register_3_q), .in3(register_4_q), .in4(register_5_q),
    .in5(register_6_q), .in6(register_7_q), .in7(register_8_q), .in8(register_9_q), .in9(register_10_q),
    .in10(register_11_q), .in11(register_12_q), .in12(register_13_q), .in13(register_14_q),
    .in14(register_15_q), .in15(register_16_q), .out(OUTA3), .sel(DA3));
  Multiplexer #(.select(4), .width(64)) multiplexer_5 (
    .in0(register_1_q), .in1(register_2_q), .in2(register_3_q), .in3(register_4_q), .in4(register_5_q),
    .in5(register_6_q), .in6(register_7_q), .in7(register_8_q), .in8(register_9_q), .in9(register_10_q),
    .in10(register_11_q), .in11(register_12_q), .in12(register_13_q), .in13(register_14_q),
    .in14(register_15_q), .in15(register_16_q), .out(OUTA4), .sel(DA4));
  Multiplexer #(.select(4), .width(64)) multiplexer_6 (
    .in0(register_1_q), .in1(register_2_q), .in2(register_3_q), .in3(register_4_q), .in4(register_5_q),
    .in5(register_6_q), .in6(register_7_q), .in7(register_8_q), .in8(register_9_q), .in9(register_10_q),
    .in10(register_11_q), .in11(register_12_q), .in12(register_13_q), .in13(register_14_q),
    .in14(register_15_q), .in15(register_16_q), .out(OUTA5), .sel(DA5));
  Multiplexer #(.select(4), .width(64)) multiplexer_7 (
    .in0(register_1_q), .in1(register_2_q), .in2(register_3_q), .in3(register_4_q), .in4(register_5_q),
    .in5(register_6_q), .in6(register_7_q), .in7(register_8_q), .in8(register_9_q), .in9(register_10_q),
    .in10(register_11_q), .in11(register_12_q), .in12(register_13_q), .in13(register_14_q),
    .in14(register_15_q), .in15(register_16_q), .out(OUTA6), .sel(DA6));
  Multiplexer #(.select(4), .width(64)) multiplexer_8 (
    .in0(register_1_q), .in1(register_2_q), .in2(register_3_q), .in3(register_4_q), .in4(register_5_q),
    .in5(register_6_q), .in6(register_7_q), .in7(register_8_q), .in8(register_9_q), .in9(register_10_q),
    .in10(register_11_q), .in11(register_12_q), .in12(register_13_q), .in13(register_14_q),
    .in14(register_15_q), .in15(register_16_q), .out(OUTA7), .sel(DA7));
  Multiplexer #(.select(4), .width(64)) multiplexer_9 (
    .in0(register_1_q), .in1(register_2_q), .in2(register_3_q), .in3(register_4_q), .in4(register_5_q),
    .in5(register_6_q), .in6(register_7_q), .in7(register_8_q), .in8(register_9_q), .in9(register_10_q),
    .in10(register_11_q), .in11(register_12_q), .in12(register_13_q), .in13(register_14_q),
    .in14(register_15_q), .in15(register_16_q), .out(OUTA8), .sel(DA8));
  Multiplexer #(.select(4), .width(64)) multiplexer_10 (
    .in0(register_1_q), .in1(register_2_q), .in2(register_3_q), .in3(register_4_q), .in4(register_5_q),
    .in5(register_6_q), .in6(register_7_q), .in7(register_8_q), .in8(register_9_q), .in9(register_10_q),
    .in10(register_11_q), .in11(register_12_q), .in12(register_13_q), .in13(register_14_q),
    .in14(register_15_q), .in15(register_16_q), .out(OUTA9), .sel(DA9));
  Multiplexer #(.select(4), .width(64)) multiplexer_11 (
    .in0(register_1_q), .in1(register_2_q), .in2(register_3_q), .in3(register_4_q), .in4(register_5_q),
    .in5(register_6_q), .in6(register_7_q), .in7(register_8_q), .in8(register_9_q), .in9(register_10_q),
    .in10(register_11_q), .in11(register_12_q), .in12(register_13_q), .in13(register_14_q),
    .in14(register_15_q), .in15(register_16_q), .out(OUTA10), .sel(DA10));
  Multiplexer #(.select(4), .width(64)) multiplexer_12 (
    .in0(register_1_q), .in1(register_2_q), .in2(register_3_q), .in3(register_4_q), .in4(register_5_q),
    .in5(register_6_q), .in6(register_7_q), .in7(register_8_q), .in8(register_9_q), .in9(register_10_q),
    .in10(register_11_q), .in11(register_12_q), .in12(register_13_q), .in13(register_14_q),
    .in14(register_15_q), .in15(register_16_q), .out(OUTA11), .sel(DA11));
  Multiplexer #(.select(4), .width(64)) multiplexer_13 (
    .in0(register_1_q), .in1(register_2_q), .in2(register_3_q), .in3(register_4_q), .in4(register_5_q),
    .in5(register_6_q), .in6(register_7_q), .in7(register_8_q), .in8(register_9_q), .in9(register_10_q),
    .in10(register_11_q), .in11(register_12_q), .in12(register_13_q), .in13(register_14_q),
    .in14(register_15_q), .in15(register_16_q), .out(OUTA12), .sel(DA12));
  Multiplexer #(.select(4), .width(64)) multiplexer_14 (
    .in0(register_1_q), .in1(register_2_q), .in2(register_3_q), .in3(register_4_q), .in4(register_5_q),
    .in5(register_6_q), .in6(register_7_q), .in7(register_8_q), .in8(register_9_q), .in9(register_10_q),
    .in10(register_11_q), .in11(register_12_q), .in12(register_13_q), .in13(register_14_q),
    .in14(register_15_q), .in15(register_16_q), .out(OUTA13), .sel(DA13));
  Multiplexer #(.select(4), .width(64)) multiplexer_15 (
    .in0(register_1_q), .in1(register_2_q), .in2(register_3_q), .in3(register_4_q), .in4(register_5_q),
    .in5(register_6_q), .in6(register_7_q), .in7(register_8_q), .in8(register_9_q), .in9(register_10_q),
    .in10(register_11_q), .in11(register_12_q), .in12(register_13_q), .in13(register_14_q),
    .in14(register_15_q), .in15(register_16_q), .out(OUTA14), .sel(DA14));
  Multiplexer #(.select(4), .width(64)) multiplexer_16 (
    .in0(register_1_q), .in1(register_2_q), .in2(register_3_q), .in3(register_4_q), .in4(register_5_q),
    .in5(register_6_q), .in6(register_7_q), .in7(register_8_q), .in8(register_9_q), .in9(register_10_q),
    .in10(register_11_q), .in11(register_12_q), .in12(register_13_q), .in13(register_14_q),
    .in14(register_15_q), .in15(register_16_q), .out(OUTA15), .sel(DA15));
  Multiplexer #(.select(4), .width(64)) multiplexer_17 (
    .in0(IN0), .in1(IN1), .in2(IN2), .in3(IN3), .in4(IN4), .in5(IN5), .in6(IN6), .in7(IN7), .in8(IN8),
    .in9(IN9), .in10(IN10), .in11(IN11), .in12(IN12), .in13(IN13), .in14(IN14), .in15(IN15),
    .out(multiplexer_17_out), .sel(A0));
  Register #(.width(64)) register_1 (
    .D(multiplexer_17_out), .en(LE0), .clk(clock_1_out), .Q(register_1_q));  // open: clr
  Clock clock_1 (.out(clock_1_out));
  Register #(.width(64)) register_2 (
    .D(multiplexer_18_out), .en(LE1), .clk(clock_2_out), .Q(register_2_q));  // open: clr
  Clock clock_2 (.out(clock_2_out));
  Multiplexer #(.select(4), .width(64)) multiplexer_18 (
    .in0(IN0), .in1(IN1), .in2(IN2), .in3(IN3), .in4(IN4), .in5(IN5), .in6(IN6), .in7(IN7), .in8(IN8),
    .in9(IN9), .in10(IN10), .in11(IN11), .in12(IN12), .in13(IN13), .in14(IN14), .in15(IN15),
    .out(multiplexer_18_out), .sel(A1));
  Multiplexer #(.select(4), .width(64)) multiplexer_19 (
    .in0(IN0), .in1(IN1), .in2(IN2), .in3(IN3), .in4(IN4), .in5(IN5), .in6(IN6), .in7(IN7), .in8(IN8),
    .in9(IN9), .in10(IN10), .in11(IN11), .in12(IN12), .in13(IN13), .in14(IN14), .in15(IN15),
    .out(multiplexer_19_out), .sel(A2));
  Register #(.width(64)) register_3 (
    .D(multiplexer_19_out), .en(LE2), .clk(clock_3_out), .Q(register_3_q));  // open: clr
  Clock clock_3 (.out(clock_3_out));
  Multiplexer #(.select(4), .width(64)) multiplexer_20 (
    .in0(IN0), .in1(IN1), .in2(IN2), .in3(IN3), .in4(IN4), .in5(IN5), .in6(IN6), .in7(IN7), .in8(IN8),
    .in9(IN9), .in10(IN10), .in11(IN11), .in12(IN12), .in13(IN13), .in14(IN14), .in15(IN15),
    .out(multiplexer_20_out), .sel(A3));
  Register #(.width(64)) register_4 (
    .D(multiplexer_20_out), .en(LE3), .clk(clock_4_out), .Q(register_4_q));  // open: clr
  Clock clock_4 (.out(clock_4_out));
  Register #(.width(64)) register_5 (
    .D(multiplexer_21_out), .en(LE4), .clk(clock_5_out), .Q(register_5_q));  // open: clr
  Clock clock_5 (.out(clock_5_out));
  Multiplexer #(.select(4), .width(64)) multiplexer_21 (
    .in0(IN0), .in1(IN1), .in2(IN2), .in3(IN3), .in4(IN4), .in5(IN5), .in6(IN6), .in7(IN7), .in8(IN8),
    .in9(IN9), .in10(IN10), .in11(IN11), .in12(IN12), .in13(IN13), .in14(IN14), .in15(IN15),
    .out(multiplexer_21_out), .sel(A4));
  Multiplexer #(.select(4), .width(64)) multiplexer_22 (
    .in0(IN0), .in1(IN1), .in2(IN2), .in3(IN3), .in4(IN4), .in5(IN5), .in6(IN6), .in7(IN7), .in8(IN8),
    .in9(IN9), .in10(IN10), .in11(IN11), .in12(IN12), .in13(IN13), .in14(IN14), .in15(IN15),
    .out(multiplexer_22_out), .sel(A5));
  Register #(.width(64)) register_6 (
    .D(multiplexer_22_out), .en(LE5), .clk(clock_6_out), .Q(register_6_q));  // open: clr
  Clock clock_6 (.out(clock_6_out));
  Register #(.width(64)) register_7 (
    .D(multiplexer_23_out), .en(LE6), .clk(clock_7_out), .Q(register_7_q));  // open: clr
  Clock clock_7 (.out(clock_7_out));
  Multiplexer #(.select(4), .width(64)) multiplexer_23 (
    .in0(IN0), .in1(IN1), .in2(IN2), .in3(IN3), .in4(IN4), .in5(IN5), .in6(IN6), .in7(IN7), .in8(IN8),
    .in9(IN9), .in10(IN10), .in11(IN11), .in12(IN12), .in13(IN13), .in14(IN14), .in15(IN15),
    .out(multiplexer_23_out), .sel(A6));
  Multiplexer #(.select(4), .width(64)) multiplexer_24 (
    .in0(IN0), .in1(IN1), .in2(IN2), .in3(IN3), .in4(IN4), .in5(IN5), .in6(IN6), .in7(IN7), .in8(IN8),
    .in9(IN9), .in10(IN10), .in11(IN11), .in12(IN12), .in13(IN13), .in14(IN14), .in15(IN15),
    .out(multiplexer_24_out), .sel(A7));
  Register #(.width(64)) register_8 (
    .D(multiplexer_24_out), .en(LE7), .clk(clock_8_out), .Q(register_8_q));  // open: clr
  Clock clock_8 (.out(clock_8_out));
  Multiplexer #(.select(4), .width(64)) multiplexer_25 (
    .in0(IN0), .in1(IN1), .in2(IN2), .in3(IN3), .in4(IN4), .in5(IN5), .in6(IN6), .in7(IN7), .in8(IN8),
    .in9(IN9), .in10(IN10), .in11(IN11), .in12(IN12), .in13(IN13), .in14(IN14), .in15(IN15),
    .out(multiplexer_25_out), .sel(A8));
  Register #(.width(64)) register_9 (
    .D(multiplexer_25_out), .en(LE8), .clk(clock_9_out), .Q(register_9_q));  // open: clr
  Clock clock_9 (.out(clock_9_out));
  Register #(.width(64)) register_10 (
    .D(multiplexer_26_out), .en(LE9), .clk(clock_10_out), .Q(register_10_q));  // open: clr
  Clock clock_10 (.out(clock_10_out));
  Multiplexer #(.select(4), .width(64)) multiplexer_26 (
    .in0(IN0), .in1(IN1), .in2(IN2), .in3(IN3), .in4(IN4), .in5(IN5), .in6(IN6), .in7(IN7), .in8(IN8),
    .in9(IN9), .in10(IN10), .in11(IN11), .in12(IN12), .in13(IN13), .in14(IN14), .in15(IN15),
    .out(multiplexer_26_out), .sel(A9));
  Multiplexer #(.select(4), .width(64)) multiplexer_27 (
    .in0(IN0), .in1(IN1), .in2(IN2), .in3(IN3), .in4(IN4), .in5(IN5), .in6(IN6), .in7(IN7), .in8(IN8),
    .in9(IN9), .in10(IN10), .in11(IN11), .in12(IN12), .in13(IN13), .in14(IN14), .in15(IN15),
    .out(multiplexer_27_out), .sel(A10));
  Register #(.width(64)) register_11 (
    .D(multiplexer_27_out), .en(LE10), .clk(clock_11_out), .Q(register_11_q));  // open: clr
  Clock clock_11 (.out(clock_11_out));
  Multiplexer #(.select(4), .width(64)) multiplexer_28 (
    .in0(IN0), .in1(IN1), .in2(IN2), .in3(IN3), .in4(IN4), .in5(IN5), .in6(IN6), .in7(IN7), .in8(IN8),
    .in9(IN9), .in10(IN10), .in11(IN11), .in12(IN12), .in13(IN13), .in14(IN14), .in15(IN15),
    .out(multiplexer_28_out), .sel(A11));
  Register #(.width(64)) register_12 (
    .D(multiplexer_28_out), .en(LE11), .clk(clock_12_out), .Q(register_12_q));  // open: clr
  Clock clock_12 (.out(clock_12_out));
  Register #(.width(64)) register_13 (
    .D(multiplexer_29_out), .en(LE12), .clk(clock_13_out), .Q(register_13_q));  // open: clr
  Clock clock_13 (.out(clock_13_out));
  Multiplexer #(.select(4), .width(64)) multiplexer_29 (
    .in0(IN0), .in1(IN1), .in2(IN2), .in3(IN3), .in4(IN4), .in5(IN5), .in6(IN6), .in7(IN7), .in8(IN8),
    .in9(IN9), .in10(IN10), .in11(IN11), .in12(IN12), .in13(IN13), .in14(IN14), .in15(IN15),
    .out(multiplexer_29_out), .sel(A12));
  Multiplexer #(.select(4), .width(64)) multiplexer_30 (
    .in0(IN0), .in1(IN1), .in2(IN2), .in3(IN3), .in4(IN4), .in5(IN5), .in6(IN6), .in7(IN7), .in8(IN8),
    .in9(IN9), .in10(IN10), .in11(IN11), .in12(IN12), .in13(IN13), .in14(IN14), .in15(IN15),
    .out(multiplexer_30_out), .sel(A13));
  Register #(.width(64)) register_14 (
    .D(multiplexer_30_out), .en(LE13), .clk(clock_14_out), .Q(register_14_q));  // open: clr
  Clock clock_14 (.out(clock_14_out));
  Register #(.width(64)) register_15 (
    .D(multiplexer_31_out), .en(LE14), .clk(clock_15_out), .Q(register_15_q));  // open: clr
  Clock clock_15 (.out(clock_15_out));
  Multiplexer #(.select(4), .width(64)) multiplexer_31 (
    .in0(IN0), .in1(IN1), .in2(IN2), .in3(IN3), .in4(IN4), .in5(IN5), .in6(IN6), .in7(IN7), .in8(IN8),
    .in9(IN9), .in10(IN10), .in11(IN11), .in12(IN12), .in13(IN13), .in14(IN14), .in15(IN15),
    .out(multiplexer_31_out), .sel(A14));
  Multiplexer #(.select(4), .width(64)) multiplexer_32 (
    .in0(IN0), .in1(IN1), .in2(IN2), .in3(IN3), .in4(IN4), .in5(IN5), .in6(IN6), .in7(IN7), .in8(IN8),
    .in9(IN9), .in10(IN10), .in11(IN11), .in12(IN12), .in13(IN13), .in14(IN14), .in15(IN15),
    .out(multiplexer_32_out), .sel(A15));
  Register #(.width(64)) register_16 (
    .D(multiplexer_32_out), .en(LE15), .clk(clock_16_out), .Q(register_16_q));  // open: clr
  Clock clock_16 (.out(clock_16_out));
  Multiplexer #(.select(4), .width(64)) multiplexer_33 (
    .in0(register_1_q), .in1(register_2_q), .in2(register_3_q), .in3(register_4_q), .in4(register_5_q),
    .in5(register_6_q), .in6(register_7_q), .in7(register_8_q), .in8(register_9_q), .in9(register_10_q),
    .in10(register_11_q), .in11(register_12_q), .in12(register_13_q), .in13(register_14_q),
    .in14(register_15_q), .in15(register_16_q), .out(OUTB0), .sel(DB0));
  Multiplexer #(.select(4), .width(64)) multiplexer_34 (
    .in0(register_1_q), .in1(register_2_q), .in2(register_3_q), .in3(register_4_q), .in4(register_5_q),
    .in5(register_6_q), .in6(register_7_q), .in7(register_8_q), .in8(register_9_q), .in9(register_10_q),
    .in10(register_11_q), .in11(register_12_q), .in12(register_13_q), .in13(register_14_q),
    .in14(register_15_q), .in15(register_16_q), .out(OUTB1), .sel(DB1));
  Multiplexer #(.select(4), .width(64)) multiplexer_35 (
    .in0(register_1_q), .in1(register_2_q), .in2(register_3_q), .in3(register_4_q), .in4(register_5_q),
    .in5(register_6_q), .in6(register_7_q), .in7(register_8_q), .in8(register_9_q), .in9(register_10_q),
    .in10(register_11_q), .in11(register_12_q), .in12(register_13_q), .in13(register_14_q),
    .in14(register_15_q), .in15(register_16_q), .out(OUTB2), .sel(DB2));
  Multiplexer #(.select(4), .width(64)) multiplexer_36 (
    .in0(register_1_q), .in1(register_2_q), .in2(register_3_q), .in3(register_4_q), .in4(register_5_q),
    .in5(register_6_q), .in6(register_7_q), .in7(register_8_q), .in8(register_9_q), .in9(register_10_q),
    .in10(register_11_q), .in11(register_12_q), .in12(register_13_q), .in13(register_14_q),
    .in14(register_15_q), .in15(register_16_q), .out(OUTB3), .sel(DB3));
  Multiplexer #(.select(4), .width(64)) multiplexer_37 (
    .in0(register_1_q), .in1(register_2_q), .in2(register_3_q), .in3(register_4_q), .in4(register_5_q),
    .in5(register_6_q), .in6(register_7_q), .in7(register_8_q), .in8(register_9_q), .in9(register_10_q),
    .in10(register_11_q), .in11(register_12_q), .in12(register_13_q), .in13(register_14_q),
    .in14(register_15_q), .in15(register_16_q), .out(OUTB4), .sel(DB4));
  Multiplexer #(.select(4), .width(64)) multiplexer_38 (
    .in0(register_1_q), .in1(register_2_q), .in2(register_3_q), .in3(register_4_q), .in4(register_5_q),
    .in5(register_6_q), .in6(register_7_q), .in7(register_8_q), .in8(register_9_q), .in9(register_10_q),
    .in10(register_11_q), .in11(register_12_q), .in12(register_13_q), .in13(register_14_q),
    .in14(register_15_q), .in15(register_16_q), .out(OUTB5), .sel(DB5));
  Multiplexer #(.select(4), .width(64)) multiplexer_39 (
    .in0(register_1_q), .in1(register_2_q), .in2(register_3_q), .in3(register_4_q), .in4(register_5_q),
    .in5(register_6_q), .in6(register_7_q), .in7(register_8_q), .in8(register_9_q), .in9(register_10_q),
    .in10(register_11_q), .in11(register_12_q), .in12(register_13_q), .in13(register_14_q),
    .in14(register_15_q), .in15(register_16_q), .out(OUTB6), .sel(DB6));
  Multiplexer #(.select(4), .width(64)) multiplexer_40 (
    .in0(register_1_q), .in1(register_2_q), .in2(register_3_q), .in3(register_4_q), .in4(register_5_q),
    .in5(register_6_q), .in6(register_7_q), .in7(register_8_q), .in8(register_9_q), .in9(register_10_q),
    .in10(register_11_q), .in11(register_12_q), .in12(register_13_q), .in13(register_14_q),
    .in14(register_15_q), .in15(register_16_q), .out(OUTB7), .sel(DB7));
  Multiplexer #(.select(4), .width(64)) multiplexer_41 (
    .in0(register_1_q), .in1(register_2_q), .in2(register_3_q), .in3(register_4_q), .in4(register_5_q),
    .in5(register_6_q), .in6(register_7_q), .in7(register_8_q), .in8(register_9_q), .in9(register_10_q),
    .in10(register_11_q), .in11(register_12_q), .in12(register_13_q), .in13(register_14_q),
    .in14(register_15_q), .in15(register_16_q), .out(OUTB8), .sel(DB8));
  Multiplexer #(.select(4), .width(64)) multiplexer_42 (
    .in0(register_1_q), .in1(register_2_q), .in2(register_3_q), .in3(register_4_q), .in4(register_5_q),
    .in5(register_6_q), .in6(register_7_q), .in7(register_8_q), .in8(register_9_q), .in9(register_10_q),
    .in10(register_11_q), .in11(register_12_q), .in12(register_13_q), .in13(register_14_q),
    .in14(register_15_q), .in15(register_16_q), .out(OUTB9), .sel(DB9));
  Multiplexer #(.select(4), .width(64)) multiplexer_43 (
    .in0(register_1_q), .in1(register_2_q), .in2(register_3_q), .in3(register_4_q), .in4(register_5_q),
    .in5(register_6_q), .in6(register_7_q), .in7(register_8_q), .in8(register_9_q), .in9(register_10_q),
    .in10(register_11_q), .in11(register_12_q), .in12(register_13_q), .in13(register_14_q),
    .in14(register_15_q), .in15(register_16_q), .out(OUTB10), .sel(DB10));
  Multiplexer #(.select(4), .width(64)) multiplexer_44 (
    .in0(register_1_q), .in1(register_2_q), .in2(register_3_q), .in3(register_4_q), .in4(register_5_q),
    .in5(register_6_q), .in6(register_7_q), .in7(register_8_q), .in8(register_9_q), .in9(register_10_q),
    .in10(register_11_q), .in11(register_12_q), .in12(register_13_q), .in13(register_14_q),
    .in14(register_15_q), .in15(register_16_q), .out(OUTB11), .sel(DB11));
  Multiplexer #(.select(4), .width(64)) multiplexer_45 (
    .in0(register_1_q), .in1(register_2_q), .in2(register_3_q), .in3(register_4_q), .in4(register_5_q),
    .in5(register_6_q), .in6(register_7_q), .in7(register_8_q), .in8(register_9_q), .in9(register_10_q),
    .in10(register_11_q), .in11(register_12_q), .in12(register_13_q), .in13(register_14_q),
    .in14(register_15_q), .in15(register_16_q), .out(OUTB12), .sel(DB12));
  Multiplexer #(.select(4), .width(64)) multiplexer_46 (
    .in0(register_1_q), .in1(register_2_q), .in2(register_3_q), .in3(register_4_q), .in4(register_5_q),
    .in5(register_6_q), .in6(register_7_q), .in7(register_8_q), .in8(register_9_q), .in9(register_10_q),
    .in10(register_11_q), .in11(register_12_q), .in12(register_13_q), .in13(register_14_q),
    .in14(register_15_q), .in15(register_16_q), .out(OUTB13), .sel(DB13));
  Multiplexer #(.select(4), .width(64)) multiplexer_47 (
    .in0(register_1_q), .in1(register_2_q), .in2(register_3_q), .in3(register_4_q), .in4(register_5_q),
    .in5(register_6_q), .in6(register_7_q), .in7(register_8_q), .in8(register_9_q), .in9(register_10_q),
    .in10(register_11_q), .in11(register_12_q), .in12(register_13_q), .in13(register_14_q),
    .in14(register_15_q), .in15(register_16_q), .out(OUTB14), .sel(DB14));
  Multiplexer #(.select(4), .width(64)) multiplexer_48 (
    .in0(register_1_q), .in1(register_2_q), .in2(register_3_q), .in3(register_4_q), .in4(register_5_q),
    .in5(register_6_q), .in6(register_7_q), .in7(register_8_q), .in8(register_9_q), .in9(register_10_q),
    .in10(register_11_q), .in11(register_12_q), .in12(register_13_q), .in13(register_14_q),
    .in14(register_15_q), .in15(register_16_q), .out(OUTB15), .sel(DB15));
endmodule
